// Logisim project LoongArch_SoC.circ as structural Verilog: 17 circuits, main circuit SoC
module SoC (
);

  wire clk, continue_out, cpu_1_out_5, debug_1_clk_o, halt, iobus_1_ioen, iobus_1_memr;
  wire [3:0] cpu_1_out_6, digitdriver_1_d0, digitdriver_1_d1, digitdriver_1_d2, digitdriver_1_d3,
       digitdriver_1_d4, digitdriver_1_d5, digitdriver_1_d6, digitdriver_1_d7, iobus_1_memw, iobus_1_out_8;
  wire [11:0] iobus_1_ioaddr12;
  wire [15:0] MissNumber;
  wire [23:0] leddriver_1_led0, undriven;
  wire [31:0] cpu_1_out_16, cpu_1_out_17, cpu_1_out_18, dram_1_read_data, iobus_1_iowritedata,
       iobus_1_memaddr, iobus_1_memwritedata, iobus_1_readdata, irom_1_instruction, switchdriver_1_ioreaddata;

  Hex_Digit_Display hex_digit_display_1 (.value(digitdriver_1_d7));  // open: dp
  Hex_Digit_Display hex_digit_display_2 (.value(digitdriver_1_d6));  // open: dp
  Hex_Digit_Display hex_digit_display_3 (.value(digitdriver_1_d5));  // open: dp
  Clock #(.highDuration(1), .lowDuration(1)) clock_1 (.out(clk));
  Hex_Digit_Display hex_digit_display_4 (.value(digitdriver_1_d3));  // open: dp
  Hex_Digit_Display hex_digit_display_5 (.value(digitdriver_1_d4));  // open: dp
  Hex_Digit_Display hex_digit_display_6 (.value(digitdriver_1_d2));  // open: dp
  Hex_Digit_Display hex_digit_display_7 (.value(digitdriver_1_d1));  // open: dp
  DigitDriver digitdriver_1 (
    .in_1(clk), .IOEn(iobus_1_ioen), .IOWriteData(iobus_1_iowritedata), .IOAddr12(iobus_1_ioaddr12),
    .D0(digitdriver_1_d0), .D4(digitdriver_1_d4), .D1(digitdriver_1_d1), .D5(digitdriver_1_d5),
    .D2(digitdriver_1_d2), .D6(digitdriver_1_d6), .D3(digitdriver_1_d3), .D7(digitdriver_1_d7),
    .IOWe(iobus_1_out_8));
  Hex_Digit_Display hex_digit_display_8 (.value(digitdriver_1_d0));  // open: dp
  // Probe on cpu_1_out_16
  IROM irom_1 (.Program_counter(cpu_1_out_16), .Instruction(irom_1_instruction));
  // Probe on irom_1_instruction
  Button \continue  (.out(continue_out));
  LED #(.active("true")) _21 (.in(leddriver_1_led0[21]));
  LED #(.active("true")) _22 (.in(leddriver_1_led0[22]));
  LED #(.active("true")) _23 (.in(leddriver_1_led0[23]));
  debug debug_1 (.PC(cpu_1_out_16), .brkPC(32'h200), .clr(continue_out), .clk_i(clk), .clk_o(debug_1_clk_o));
  LED #(.active("true")) _20 (.in(leddriver_1_led0[20]));
  LED #(.active("true")) _17 (.in(leddriver_1_led0[17]));
  LED #(.active("true")) _18 (.in(leddriver_1_led0[18]));
  LED #(.active("true")) _19 (.in(leddriver_1_led0[19]));
  LEDDriver leddriver_1 (
    .in_1(clk), .IOEn(iobus_1_ioen), .IOWriteData(iobus_1_iowritedata), .IOAddr12(iobus_1_ioaddr12),
    .LED0(leddriver_1_led0), .IOWe(iobus_1_out_8));
  LED #(.active("true")) _14 (.in(leddriver_1_led0[14]));
  LED #(.active("true")) _15 (.in(leddriver_1_led0[15]));
  LED #(.active("true")) _16 (.in(leddriver_1_led0[16]));
  LED #(.active("true")) _13 (.in(leddriver_1_led0[13]));
  LED #(.active("true")) _11 (.in(leddriver_1_led0[11]));
  LED #(.active("true")) _12 (.in(leddriver_1_led0[12]));
  LED #(.active("true")) _9 (.in(leddriver_1_led0[9]));
  LED #(.active("true")) _10 (.in(leddriver_1_led0[10]));
  LED #(.active("true")) _8 (.in(leddriver_1_led0[8]));
  LED #(.active("true")) _6 (.in(leddriver_1_led0[6]));
  LED #(.active("true")) _5 (.in(leddriver_1_led0[5]));
  LED #(.active("true")) _7 (.in(leddriver_1_led0[7]));
  CPU cpu_1 (
    .in_3(debug_1_clk_o), .in_1(irom_1_instruction), .out_16(cpu_1_out_16), .out_17(cpu_1_out_17),
    .out_18(cpu_1_out_18), .out_5(cpu_1_out_5), .in_2(iobus_1_readdata), .out_6(cpu_1_out_6), .out_7(halt));  // open: out_9, out_13, out_8, out_10, out_15, out_11, out_14, out_12, in_4
  LED #(.active("true")) _1 (.in(leddriver_1_led0[1]));
  LED #(.active("true")) _4 (.in(leddriver_1_led0[4]));
  LED #(.active("true")) _2 (.in(leddriver_1_led0[2]));
  LED #(.active("true")) _3 (.in(leddriver_1_led0[3]));
  // DipSwitch #(.NSwitches(24)) dipswitch_1: pin names not known; wires that end beside it: undriven[23], undriven[22], undriven[21], undriven[20], undriven[19], undriven[18], undriven[17], undriven[16], undriven[15], undriven[14], undriven[13], undriven[12]
  LED #(.active("true")) _0 (.in(leddriver_1_led0[0]));
  IOBus iobus_1 (
    .R(cpu_1_out_5), .IOEn(iobus_1_ioen), .ReadData(iobus_1_readdata), .IOAddr12(iobus_1_ioaddr12),
    .IOReadData(switchdriver_1_ioreaddata), .WriteAddr(cpu_1_out_17), .WriteData(cpu_1_out_18),
    .MemRead(dram_1_read_data), .IOWriteData(iobus_1_iowritedata), .MemAddr(iobus_1_memaddr),
    .MemR(iobus_1_memr), .MemWriteData(iobus_1_memwritedata), .out_8(iobus_1_out_8), .W(cpu_1_out_6),
    .MemW(iobus_1_memw));
  SwitchDriver switchdriver_1 (
    .in_1(clk), .SW0(undriven), .IOEn(iobus_1_ioen), .IOAddr12(iobus_1_ioaddr12),
    .IOReadData(switchdriver_1_ioreaddata));
  DRAM dram_1 (
    .Write_En(iobus_1_memw), .clk(clk), .Read_Data(dram_1_read_data), .Address(iobus_1_memaddr),
    .Write_Data(iobus_1_memwritedata), .Read_En(iobus_1_memr), .MissNubmer(MissNumber));
  Timer timer_1 (
    .in_1(clk), .IOEn(iobus_1_ioen), .IOWriteData(iobus_1_iowritedata), .IOWe(iobus_1_out_8),
    .IOAddr12(iobus_1_ioaddr12), .IOReadData(switchdriver_1_ioreaddata));

  // Notes on the sheet:
  //   DK7
  //   DK5
  //   DK6
  //   DK3
  //   DK4
  //   时钟
  //   DK1
  //   DK2
  //   DK0
  //   23
  //   I/O总线
  //   20
  //   22
  //   21
  //   19
  //   17
  //   16
  //   15
  //   18
  //   11
  //   14
  //   13
  //   12
  //   8
  //   7
  //   10
  //   9
  //   3
  //   6
  //   4
  //   5
  //   2
  //   0
  //   1
endmodule

module CPU (
  input  [31:0] in_1,
  input  [31:0] in_2,
  input  in_3,
  input  in_4,
  output out_5,
  output [3:0] out_6,
  output out_7,
  output [31:0] out_8,
  output [31:0] out_9,
  output [31:0] out_10,
  output [31:0] out_11,
  output [31:0] out_12,
  output [31:0] out_13,
  output [31:0] out_14,
  output [31:0] out_15,
  output [31:0] out_16,
  output [31:0] out_17,
  output [31:0] out_18
);

  wire and_1_out, and_2_out, and_3_out, and_4_out, Branch, branch_1_breq, branch_1_brlt,
       controlmodel_1_alusela, controlmodel_1_aluselb, controlmodel_1_beq, controlmodel_1_bge,
       controlmodel_1_bgeu, controlmodel_1_bl, controlmodel_1_blt, controlmodel_1_bltu, controlmodel_1_bne,
       controlmodel_1_brun, controlmodel_1_pcsel, controlmodel_1_rdsel, controlmodel_1_regwrite, En,
       load_sign, or_1_out, or_2_out;
  wire [1:0] controlmodel_1_wbsel;
  wire [2:0] controlmodel_1_immsel;
  wire [3:0] controlmodel_1_aluop, MemR;
  wire [4:0] multiplexer_2_out, multiplexer_3_out;
  wire [31:0] adder_1_out, immmodel_1_imm_out, multiplexer_1_out, multiplexer_4_out, multiplexer_5_out,
       multiplexer_6_out, regfile_1_read_data_1, w2borh_1_dout;

  // Probe on adder_1_out
  Adder #(.width(32)) adder_1 (.a(out_16), .b(32'h4), .out(adder_1_out));  // open: cin, cout
  Multiplexer #(.select(1), .width(32), .disabled("Z"), .enable("false")) multiplexer_1 (
    .in0(adder_1_out), .in1(out_17), .out(multiplexer_1_out), .sel(Branch));
  // Probe on out_16
  Register #(.width(32), .trigger("rising"), .Select("low")) PC (
    .D(multiplexer_1_out), .en(En), .Q(out_16), .clk(in_3));  // open: clr
  nor nor_1 (En, out_7, in_4);
  Comparator #(.width(32), .mode("unsigned")) comparator_1 (.a(in_1), .b({32{1'b0}}), .eq(out_7));  // open: gt, lt
  Pull_Resistor #(.pull(0)) pull_resistor_1 (.node(in_4));
  // Probe on in_1
  Multiplexer #(.select(1), .width(5), .disabled("Z"), .enable("false")) multiplexer_2 (
    .in0(in_1[4:0]), .in1(5'b00001), .out(multiplexer_2_out), .sel(controlmodel_1_bl));
  Multiplexer #(.select(1), .width(5), .disabled("Z"), .enable("false")) multiplexer_3 (
    .in0(in_1[14:10]), .in1(multiplexer_2_out), .out(multiplexer_3_out), .sel(controlmodel_1_rdsel));
  // Probe on multiplexer_6_out
  ControlModel controlmodel_1 (
    .ALUSelB(controlmodel_1_aluselb), .MemWrite(out_6), .ALUSelA(controlmodel_1_alusela),
    .PCSel(controlmodel_1_pcsel), .WBSel(controlmodel_1_wbsel), .MemRead(MemR), .BEQ(controlmodel_1_beq),
    .BNE(controlmodel_1_bne), .BGE(controlmodel_1_bge), .BLT(controlmodel_1_blt), .BLTU(controlmodel_1_bltu),
    .BGEU(controlmodel_1_bgeu), .offset(out_17[1:0]), .opcode(in_1[31:15]), .ImmSel(controlmodel_1_immsel),
    .RegWrite(controlmodel_1_regwrite), .BrUN(controlmodel_1_brun), .LoadSign(load_sign),
    .ALUOP(controlmodel_1_aluop), .rdSel(controlmodel_1_rdsel), .bl(controlmodel_1_bl));
  ImmModel immmodel_1 (.Imm_out(immmodel_1_imm_out), .ImmSel(controlmodel_1_immsel), .Imm_in(in_1[25:0]));
  RegFile regfile_1 (
    .rs1(in_1[9:5]), .rs2(multiplexer_3_out), .rd(multiplexer_2_out), .Write_Data(multiplexer_6_out),
    .RegWE(controlmodel_1_regwrite), .clk(in_3), .Read_Data_1(regfile_1_read_data_1), .Read_Data_2(out_18),
    .ra(out_8), .sp(out_9), .t0(out_10), .t1(out_11), .t2(out_12), .s0(out_13), .s1(out_14), .a0(out_15));
  // Probe on out_18
  or or_1 (or_1_out, controlmodel_1_bge, controlmodel_1_bgeu);
  // Probe on immmodel_1_imm_out
  or or_2 (or_2_out, controlmodel_1_blt, controlmodel_1_bltu);
  Branch branch_1 (
    .BrEQ(branch_1_breq), .BrUN(controlmodel_1_brun), .Rj(regfile_1_read_data_1), .BrLT(branch_1_brlt),
    .Rd(out_18));
  Multiplexer #(.select(1), .width(32), .disabled("Z"), .enable("false")) multiplexer_4 (
    .in0(regfile_1_read_data_1), .in1(out_16), .out(multiplexer_4_out), .sel(controlmodel_1_alusela));
  Multiplexer #(.select(1), .width(32), .disabled("Z"), .enable("false")) multiplexer_5 (
    .in0(out_18), .in1(immmodel_1_imm_out), .out(multiplexer_5_out), .sel(controlmodel_1_aluselb));
  and and_1 (and_1_out, branch_1_breq, controlmodel_1_beq);
  and and_2 (and_2_out, ~branch_1_breq, controlmodel_1_bne);  // AND_Gate
  and and_3 (and_3_out, branch_1_brlt, or_2_out);
  and and_4 (and_4_out, ~branch_1_brlt, or_1_out);  // AND_Gate
  or or_3 (Branch, controlmodel_1_pcsel, and_1_out, and_2_out, and_3_out, and_4_out);
  // Probe on out_17
  AluModel alumodel_1 (.ALUSel(controlmodel_1_aluop), .A(multiplexer_4_out), .B(multiplexer_5_out), .Result(out_17));
  or or_4 (out_5, MemR[0], MemR[1], MemR[2], MemR[3]);
  W2BorH w2borh_1 (.din(in_2), .mask(MemR), .dout(w2borh_1_dout), .\signed (load_sign));
  // Probe on w2borh_1_dout
  Multiplexer #(.select(2), .width(32), .disabled("Z"), .enable("false")) multiplexer_6 (
    .in0(adder_1_out), .in1(out_17), .in2(w2borh_1_dout), .out(multiplexer_6_out), .sel(controlmodel_1_wbsel));  // open: in3

  // Other names for the same wires on the sheet: a0[31:0] = out_15; clk = in_3; fetch_addr[31:0] = out_16;
  //   halt = out_7; Instruction[31:0] = in_1; MemR1 = out_5; MemW[3:0] = out_6; Miss = in_4; ra[31:0] = out_8;
  //   ReadData[31:0] = in_2; s0[31:0] = out_13; s1[31:0] = out_14; sp[31:0] = out_9; t0[31:0] = out_10;
  //   t1[31:0] = out_11; t2[31:0] = out_12; WriteAddr[31:0] = out_17; WriteData[31:0] = out_18

  // Notes on the sheet:
  //   PC
  //   PC+4
  //   ALU_Result
  //   ALU_Result
  //   输入引脚区
  //   ALU_Result
  //   输出引脚区
  //   PC+4
  //   WriteData
  //   WBSel
endmodule

module ControlModel (
  input  [16:0] opcode,
  input  [1:0] offset,
  output BEQ,
  output BNE,
  output BLT,
  output BLTU,
  output BGE,
  output BGEU,
  output BrUN,
  output LoadSign,
  output bl,
  output PCSel,
  output RegWrite,
  output [2:0] ImmSel,
  output rdSel,
  output [1:0] WBSel,
  output [3:0] MemWrite,
  output ALUSelA,
  output [3:0] ALUOP,
  output ALUSelB,
  output [3:0] MemRead
);

  wire _1RI20, _2RI5, _2RI12, _2RI12_ld_st, _2RI12_ldu, _2RI12_logic, _2RI12_st, _2RI16, _3R, and_1_out,
       and_2_out, and_7_out, and_8_out, and_11_out, and_12_out, andi, b, I26, jirl, ld_b, ld_bu, ld_h, ld_hu,
       ld_w, lu12i_w, mem_load, opc1_0, opc1_1, opc3_0, opc3_1, opc3_2, opc3_4, opc3_5, opc3_6, opc3_7,
       opc6_00, opc6_0a, opc6_07, or_1_out, or_5_out, or_6_out, or_12_out, or_13_out, or_14_out, or_16_out,
       or_18_out, ori, st_b, st_h, st_w, xori;
  wire [2:0] multiplexer_1_out;
  wire [3:0] AOP_2RI5, AOP_2RI12, AOP_3R, decoder_1_out0, decoder_2_out0, decoder_4_out0, decoder_5_out0;

  or or_1 (or_1_out, andi, ori, xori);
  and and_1 (and_1_out, _2RI16, ~jirl);  // AND_Gate
  not not_1 (opc1_1, opc1_0);
  Comparator #(.width(1), .mode("unsigned")) comparator_1 (.a(opcode[10]), .b(1'b0), .eq(opc1_0));  // open: gt, lt
  Comparator #(.width(3), .mode("unsigned")) comparator_2 (.a(opcode[9:7]), .b(3'b000), .eq(opc3_0));  // open: gt, lt
  Comparator #(.width(3), .mode("unsigned")) comparator_3 (.a(opcode[9:7]), .b(3'b001), .eq(opc3_1));  // open: gt, lt
  Comparator #(.width(3), .mode("unsigned")) comparator_4 (.a(opcode[9:7]), .b(3'b010), .eq(opc3_2));  // open: gt, lt
  Comparator #(.width(3), .mode("unsigned")) comparator_5 (.a(opcode[9:7]), .b(3'b100), .eq(opc3_4));  // open: gt, lt
  Comparator #(.width(3), .mode("unsigned")) comparator_6 (.a(opcode[9:7]), .b(3'b101), .eq(opc3_5));  // open: gt, lt
  Comparator #(.width(3), .mode("unsigned")) comparator_7 (.a(opcode[9:7]), .b(3'b110), .eq(opc3_6));  // open: gt, lt
  Comparator #(.width(3), .mode("unsigned")) comparator_8 (.a(opcode[9:7]), .b(3'b111), .eq(opc3_7));  // open: gt, lt
  Priority_Encoder #(.select(3), .disabled("Z")) priority_encoder_1 (
    .in0(_2RI5), .in1(or_1_out), .in2(_2RI12), .in3(_1RI20), .in4(_2RI16), .in5(I26), .out(ImmSel),
    .en_in(1'b1));  // open: in6, in7, gs, en_out
  or or_2 (ALUSelA, _1RI20, and_1_out, I26);
  or or_3 (ALUSelB, _2RI5, _2RI12, _1RI20, _2RI16, I26);
  and and_2 (and_2_out, _2RI16, ~jirl);  // AND_Gate
  Comparator #(.width(6), .mode("unsigned")) comparator_9 (
    .a(opcode[16:11]), .b({6{1'b0}}), .eq(opc6_00));  // open: gt, lt
  Comparator #(.width(6), .mode("unsigned")) comparator_10 (
    .a(opcode[16:11]), .b(6'b001010), .eq(opc6_0a));  // open: gt, lt
  Comparator #(.width(6), .mode("unsigned")) comparator_11 (
    .a(opcode[16:11]), .b(6'b000101), .eq(lu12i_w));  // open: gt, lt
  Comparator #(.width(6), .mode("unsigned")) comparator_12 (
    .a(opcode[16:11]), .b(6'b000111), .eq(opc6_07));  // open: gt, lt
  Comparator #(.width(6), .mode("unsigned")) comparator_13 (
    .a(opcode[16:11]), .b(6'b010110), .eq(BEQ));  // open: gt, lt
  Comparator #(.width(6), .mode("unsigned")) comparator_14 (
    .a(opcode[16:11]), .b(6'b010111), .eq(BNE));  // open: gt, lt
  Comparator #(.width(6), .mode("unsigned")) comparator_15 (
    .a(opcode[16:11]), .b(6'b011000), .eq(BLT));  // open: gt, lt
  Comparator #(.width(6), .mode("unsigned")) comparator_16 (
    .a(opcode[16:11]), .b(6'b011001), .eq(BGE));  // open: gt, lt
  Comparator #(.width(6), .mode("unsigned")) comparator_17 (
    .a(opcode[16:11]), .b(6'b011010), .eq(BLTU));  // open: gt, lt
  Comparator #(.width(6), .mode("unsigned")) comparator_18 (
    .a(opcode[16:11]), .b(6'b011011), .eq(BGEU));  // open: gt, lt
  Comparator #(.width(6), .mode("unsigned")) comparator_19 (
    .a(opcode[16:11]), .b(6'b010011), .eq(jirl));  // open: gt, lt
  Comparator #(.width(6), .mode("unsigned")) comparator_20 (.a(opcode[16:11]), .b(6'b010100), .eq(b));  // open: gt, lt
  Comparator #(.width(6), .mode("unsigned")) comparator_21 (.a(opcode[16:11]), .b(6'b010101), .eq(bl));  // open: gt, lt
  nor nor_1 (RegWrite, _2RI12_st, and_2_out, b);
  or or_4 (rdSel, and_2_out, _2RI12_st);
  Decoder #(.select(2), .tristate("false"), .disabled(0), .enable("true")) decoder_1 (
    .out0(decoder_1_out0[0]), .out1(decoder_1_out0[1]), .out2(decoder_1_out0[2]), .out3(decoder_1_out0[3]),
    .sel(offset), .en(mem_load));
  Decoder #(.select(1), .tristate("false"), .disabled(0), .enable("true")) decoder_2 (
    .out0(decoder_2_out0[0]), .out1(decoder_2_out0[2]), .sel(offset[1]), .en(mem_load));
  Decoder #(.select(1), .tristate("false"), .disabled(0), .enable("true")) decoder_3 (
    .out0(decoder_2_out0[1]), .out1(decoder_2_out0[3]), .sel(offset[1]), .en(mem_load));
  Decoder #(.select(2), .tristate("false"), .disabled(0), .enable("true")) decoder_4 (
    .out0(decoder_4_out0[0]), .out1(decoder_4_out0[1]), .out2(decoder_4_out0[2]), .out3(decoder_4_out0[3]),
    .sel(offset), .en(_2RI12_st));
  Decoder #(.select(1), .tristate("false"), .disabled(0), .enable("true")) decoder_5 (
    .out0(decoder_5_out0[0]), .out1(decoder_5_out0[2]), .sel(offset[1]), .en(_2RI12_st));
  Decoder #(.select(1), .tristate("false"), .disabled(0), .enable("true")) decoder_6 (
    .out0(decoder_5_out0[1]), .out1(decoder_5_out0[3]), .sel(offset[1]), .en(_2RI12_st));
  assign MemWrite = st_b ? decoder_4_out0 : 4'bz;  // Controlled_Buffer controlled_buffer_1
  assign MemWrite = st_h ? decoder_5_out0 : 4'bz;  // Controlled_Buffer controlled_buffer_2
  assign MemWrite = st_w ? 4'b1111 : 4'bz;  // Controlled_Buffer controlled_buffer_3
  or or_5 (or_5_out, ld_b, ld_bu);
  or or_6 (or_6_out, ld_h, ld_hu);
  Pull_Resistor #(.pull(0)) pull_resistor_1 (.node(MemWrite));
  assign MemRead = or_5_out ? decoder_1_out0 : 4'bz;  // Controlled_Buffer controlled_buffer_4
  assign MemRead = or_6_out ? decoder_2_out0 : 4'bz;  // Controlled_Buffer controlled_buffer_5
  Pull_Resistor #(.pull(0)) pull_resistor_2 (.node(MemRead));
  assign MemRead = ld_w ? 4'b1111 : 4'bz;  // Controlled_Buffer controlled_buffer_6
  or or_7 (mem_load, _2RI12_ldu, LoadSign);
  and and_3 (_3R, opc6_00, opc1_0, opc3_0);
  and and_4 (_2RI5, opc6_00, opc1_0, opc3_1);
  or or_8 (_2RI12, _2RI12_logic, _2RI12_ld_st);
  or or_9 (_1RI20, lu12i_w, opc6_07);
  or or_10 (_2RI16, BEQ, BNE, BLT, BGE, BLTU, BGEU, jirl);
  or or_11 (I26, b, bl);
  Multiplexer #(.select(1), .width(3), .disabled("Z"), .enable("false")) multiplexer_1 (
    .in0(opcode[9:7]), .in1(3'b010), .out(multiplexer_1_out), .sel(or_12_out));
  or or_12 (or_12_out, _2RI12_st, mem_load);
  and and_5 (_2RI12_logic, opc6_00, opc1_1);
  and and_6 (_2RI12_ldu, opc6_0a, opc1_1);
  and and_7 (and_7_out, opc6_0a, opc1_0);
  or or_13 (or_13_out, opc3_0, opc3_1, opc3_2);
  or or_14 (or_14_out, opc3_4, opc3_5, opc3_6);
  or or_15 (PCSel, jirl, b, bl);
  and and_8 (and_8_out, _2RI12, ~or_16_out);  // AND_Gate
  or or_16 (or_16_out, mem_load, _2RI12_st);
  and and_9 (LoadSign, and_7_out, or_13_out);
  and and_10 (_2RI12_st, and_7_out, or_14_out);
  or or_17 (BrUN, BLTU, BGEU);
  or or_18 (or_18_out, _3R, _2RI5, _1RI20, and_8_out);
  ROM #(.addrWidth(7), .dataWidth(4), .Select("high")) rom_1 (.addr(opcode[6:0]), .data(AOP_3R));
  ROM #(.addrWidth(2), .dataWidth(4), .Select("high")) rom_2 (.addr(opcode[4:3]), .data(AOP_2RI5));
  ROM #(.addrWidth(3), .dataWidth(4), .Select("high")) rom_3 (.addr(multiplexer_1_out), .data(AOP_2RI12));
  or or_19 (_2RI12_ld_st, _2RI12_ldu, _2RI12_st, LoadSign);
  // Probe on PCSel
  Priority_Encoder #(.select(2), .disabled("Z")) priority_encoder_2 (
    .in0(PCSel), .in1(or_18_out), .in2(mem_load), .out(WBSel), .en_in(1'b1));  // open: in3, gs, en_out
  and and_11 (and_11_out, opc6_0a, opc1_0);
  and and_12 (and_12_out, opc6_0a, opc1_1);
  assign ALUOP = _3R ? AOP_3R : 4'bz;  // Controlled_Buffer controlled_buffer_7
  assign ALUOP = _2RI5 ? AOP_2RI5 : 4'bz;  // Controlled_Buffer controlled_buffer_8
  assign ALUOP = _2RI12 ? AOP_2RI12 : 4'bz;  // Controlled_Buffer controlled_buffer_9
  assign ALUOP = lu12i_w ? 4'b1101 : 4'bz;  // Controlled_Buffer controlled_buffer_10
  assign ALUOP = opc6_07 ? 4'b0000 : 4'bz;  // Controlled_Buffer controlled_buffer_11
  assign ALUOP = _2RI16 ? 4'b0000 : 4'bz;  // Controlled_Buffer controlled_buffer_12
  assign ALUOP = I26 ? 4'b0000 : 4'bz;  // Controlled_Buffer controlled_buffer_13
  and and_13 (andi, _2RI12_logic, opc3_5);
  and and_14 (ori, _2RI12_logic, opc3_6);
  and and_15 (xori, _2RI12_logic, opc3_7);
  and and_16 (ld_b, and_11_out, opc3_0);
  and and_17 (ld_h, and_11_out, opc3_1);
  and and_18 (ld_w, and_11_out, opc3_2);
  and and_19 (st_b, and_11_out, opc3_4);
  and and_20 (st_h, and_11_out, opc3_5);
  and and_21 (st_w, and_11_out, opc3_6);
  and and_22 (ld_bu, and_12_out, opc3_0);
  and and_23 (ld_hu, and_12_out, opc3_1);
  // Probe on ALUOP
  Pull_Resistor #(.pull(0)) pull_resistor_3 (.node(ALUOP));

  // Other names for the same wires on the sheet: _2RI12_ld = LoadSign; mem_store = _2RI12_st; off_1 = offset[1];
  //   opc6_1a = BLTU; opc6_1b = BGEU; opc6_05 = lu12i_w; opc6_13 = jirl; opc6_14 = b; opc6_15 = bl; opc6_16 = BEQ;
  //   opc6_17 = BNE; opc6_18 = BLT; opc6_19 = BGE; opc7[6:0] = opcode[6:0]; opc3[2:0] = opcode[9:7];
  //   opc1 = opcode[10]; opc6[5:0] = opcode[16:11]; pcaddu12i = opc6_07

  // Notes on the sheet:
  //   contents of rom_1 (hex, n*v repeats v):
  //   34*0 c 0 7 f 0 0 0 1 2 3 0 0 6 4 5 7*0 a e b 7*0 8 9
  //   contents of rom_2 (hex, n*v repeats v):
  //   6 4 5
  //   contents of rom_3 (hex, n*v repeats v):
  //   7 f 0 0 0 1 2 3
endmodule

module RegFile (
  input  [4:0] rs1,
  input  [4:0] rs2,
  input  [4:0] rd,
  input  [31:0] Write_Data,
  input  RegWE,
  input  clk,
  output [31:0] ra,
  output [31:0] sp,
  output [31:0] t0,
  output [31:0] t1,
  output [31:0] t2,
  output [31:0] s0,
  output [31:0] s1,
  output [31:0] a0,
  output [31:0] Read_Data_1,
  output [31:0] Read_Data_2
);

  wire write_en1, write_en2, write_en3, write_en4, write_en5, write_en6, write_en7, write_en8, write_en9,
       write_en10, write_en11, write_en12, write_en13, write_en14, write_en15, write_en16, write_en17,
       write_en18, write_en19, write_en20, write_en21, write_en22, write_en23, write_en24, write_en25,
       write_en26, write_en27, write_en28, write_en29, write_en30, write_en31;
  wire [31:0] a1, a2, a3, a4, a5, a6, a7, fp_s9, s2, s3, s4, s5, s6, s7, s8, t3, t4, t5, t6, t7, t8, tp, u0;

  Pull_Resistor #(.pull(0)) pull_resistor_1 (.node(write_en1));
  Register #(.width(32), .trigger("rising"), .Select("low")) register_1 (
    .D(Write_Data), .en(write_en8), .Q(a4), .clk(clk));  // open: clr
  Register #(.width(32), .trigger("rising"), .Select("low")) register_2 (
    .D(Write_Data), .en(write_en16), .Q(t4), .clk(clk));  // open: clr
  Register #(.width(32), .trigger("rising"), .Select("low")) register_3 (
    .D(Write_Data), .en(write_en24), .Q(s1), .clk(clk));  // open: clr
  Pull_Resistor #(.pull(0)) pull_resistor_2 (.node(write_en2));
  Pull_Resistor #(.pull(0)) pull_resistor_3 (.node(write_en3));
  Pull_Resistor #(.pull(0)) pull_resistor_4 (.node(write_en4));
  Pull_Resistor #(.pull(0)) pull_resistor_5 (.node(write_en5));
  Register #(.width(32), .trigger("rising"), .Select("low")) register_4 (
    .D(Write_Data), .en(write_en1), .Q(ra), .clk(clk));  // open: clr
  Register #(.width(32), .trigger("rising"), .Select("low")) register_5 (
    .D(Write_Data), .en(write_en9), .Q(a5), .clk(clk));  // open: clr
  Register #(.width(32), .trigger("rising"), .Select("low")) register_6 (
    .D(Write_Data), .en(write_en17), .Q(t5), .clk(clk));  // open: clr
  Register #(.width(32), .trigger("rising"), .Select("low")) register_7 (
    .D(Write_Data), .en(write_en25), .Q(s2), .clk(clk));  // open: clr
  Pull_Resistor #(.pull(0)) pull_resistor_6 (.node(write_en6));
  Pull_Resistor #(.pull(0)) pull_resistor_7 (.node(write_en7));
  // Probe on ra
  Pull_Resistor #(.pull(0)) pull_resistor_8 (.node(write_en8));
  Pull_Resistor #(.pull(0)) pull_resistor_9 (.node(write_en9));
  // Probe on Write_Data
  // Probe on write_en18
  Pull_Resistor #(.pull(0)) pull_resistor_10 (.node(write_en11));
  Pull_Resistor #(.pull(0)) pull_resistor_11 (.node(write_en10));
  Register #(.width(32), .trigger("rising"), .Select("low")) register_8 (
    .D(Write_Data), .en(write_en2), .Q(tp), .clk(clk));  // open: clr
  Register #(.width(32), .trigger("rising"), .Select("low")) register_9 (
    .D(Write_Data), .en(write_en10), .Q(a6), .clk(clk));  // open: clr
  // Probe on t6
  Register #(.width(32), .trigger("rising"), .Select("low")) register_10 (
    .D(Write_Data), .en(write_en18), .Q(t6), .clk(clk));  // open: clr
  Register #(.width(32), .trigger("rising"), .Select("low")) register_11 (
    .D(Write_Data), .en(write_en26), .Q(s3), .clk(clk));  // open: clr
  Pull_Resistor #(.pull(0)) pull_resistor_12 (.node(write_en12));
  Pull_Resistor #(.pull(0)) pull_resistor_13 (.node(write_en13));
  Pull_Resistor #(.pull(0)) pull_resistor_14 (.node(write_en14));
  Pull_Resistor #(.pull(0)) pull_resistor_15 (.node(write_en15));
  Register #(.width(32), .trigger("rising"), .Select("low")) register_12 (
    .D(Write_Data), .en(write_en3), .Q(sp), .clk(clk));  // open: clr
  Register #(.width(32), .trigger("rising"), .Select("low")) register_13 (
    .D(Write_Data), .en(write_en11), .Q(a7), .clk(clk));  // open: clr
  Register #(.width(32), .trigger("rising"), .Select("low")) register_14 (
    .D(Write_Data), .en(write_en19), .Q(t7), .clk(clk));  // open: clr
  Register #(.width(32), .trigger("rising"), .Select("low")) register_15 (
    .D(Write_Data), .en(write_en27), .Q(s4), .clk(clk));  // open: clr
  Pull_Resistor #(.pull(0)) pull_resistor_16 (.node(write_en16));
  Pull_Resistor #(.pull(0)) pull_resistor_17 (.node(write_en17));
  Decoder #(.select(5), .tristate("false"), .disabled("Z"), .enable("true")) decoder_1 (
    .out1(write_en1), .out2(write_en2), .out3(write_en3), .out4(write_en4), .out5(write_en5),
    .out6(write_en6), .out7(write_en7), .out8(write_en8), .out9(write_en9), .out10(write_en10),
    .out11(write_en11), .out12(write_en12), .out13(write_en13), .out14(write_en14), .out15(write_en15),
    .out16(write_en16), .out17(write_en17), .out18(write_en18), .out19(write_en19), .out20(write_en20),
    .out21(write_en21), .out22(write_en22), .out23(write_en23), .out24(write_en24), .out25(write_en25),
    .out26(write_en26), .out27(write_en27), .out28(write_en28), .out29(write_en29), .out30(write_en30),
    .out31(write_en31), .sel(rd), .en(RegWE));  // open: out0
  Pull_Resistor #(.pull(0)) pull_resistor_18 (.node(write_en18));
  Pull_Resistor #(.pull(0)) pull_resistor_19 (.node(write_en19));
  // Probe on rd
  Register #(.width(32), .trigger("rising"), .Select("low")) register_16 (
    .D(Write_Data), .en(write_en4), .Q(a0), .clk(clk));  // open: clr
  Register #(.width(32), .trigger("rising"), .Select("low")) register_17 (
    .D(Write_Data), .en(write_en12), .Q(t0), .clk(clk));  // open: clr
  Register #(.width(32), .trigger("rising"), .Select("low")) register_18 (
    .D(Write_Data), .en(write_en20), .Q(t8), .clk(clk));  // open: clr
  Register #(.width(32), .trigger("rising"), .Select("low")) register_19 (
    .D(Write_Data), .en(write_en28), .Q(s5), .clk(clk));  // open: clr
  Pull_Resistor #(.pull(0)) pull_resistor_20 (.node(write_en20));
  Pull_Resistor #(.pull(0)) pull_resistor_21 (.node(write_en21));
  Pull_Resistor #(.pull(0)) pull_resistor_22 (.node(write_en22));
  Pull_Resistor #(.pull(0)) pull_resistor_23 (.node(write_en23));
  Register #(.width(32), .trigger("rising"), .Select("low")) register_20 (
    .D(Write_Data), .en(write_en5), .Q(a1), .clk(clk));  // open: clr
  Register #(.width(32), .trigger("rising"), .Select("low")) register_21 (
    .D(Write_Data), .en(write_en13), .Q(t1), .clk(clk));  // open: clr
  Register #(.width(32), .trigger("rising"), .Select("low")) register_22 (
    .D(Write_Data), .en(write_en21), .Q(u0), .clk(clk));  // open: clr
  Register #(.width(32), .trigger("rising"), .Select("low")) register_23 (
    .D(Write_Data), .en(write_en29), .Q(s6), .clk(clk));  // open: clr
  Pull_Resistor #(.pull(0)) pull_resistor_24 (.node(write_en24));
  Pull_Resistor #(.pull(0)) pull_resistor_25 (.node(write_en25));
  Pull_Resistor #(.pull(0)) pull_resistor_26 (.node(write_en27));
  Pull_Resistor #(.pull(0)) pull_resistor_27 (.node(write_en26));
  // Probe on Read_Data_1
  // Probe on rs1
  Pull_Resistor #(.pull(0)) pull_resistor_28 (.node(write_en28));
  Multiplexer #(.select(5), .width(32), .disabled("Z"), .enable("false")) multiplexer_1 (
    .in0({32{1'b0}}), .in1(ra), .in2(tp), .in3(sp), .in4(a0), .in5(a1), .in6(a2), .in7(a3), .in8(a4),
    .in9(a5), .in10(a6), .in11(a7), .in12(t0), .in13(t1), .in14(t2), .in15(t3), .in16(t4), .in17(t5),
    .in18(t6), .in19(t7), .in20(t8), .in21(u0), .in22(fp_s9), .in23(s0), .in24(s1), .in25(s2), .in26(s3),
    .in27(s4), .in28(s5), .in29(s6), .in30(s7), .in31(s8), .out(Read_Data_1), .sel(rs1));
  Register #(.width(32), .trigger("rising"), .Select("low")) register_24 (
    .D(Write_Data), .en(write_en6), .Q(a2), .clk(clk));  // open: clr
  Register #(.width(32), .trigger("rising"), .Select("low")) register_25 (
    .D(Write_Data), .en(write_en14), .Q(t2), .clk(clk));  // open: clr
  Register #(.width(32), .trigger("rising"), .Select("low")) register_26 (
    .D(Write_Data), .en(write_en22), .Q(fp_s9), .clk(clk));  // open: clr
  // Probe on s7
  Register #(.width(32), .trigger("rising"), .Select("low")) register_27 (
    .D(Write_Data), .en(write_en30), .Q(s7), .clk(clk));  // open: clr
  Pull_Resistor #(.pull(0)) pull_resistor_29 (.node(write_en29));
  Pull_Resistor #(.pull(0)) pull_resistor_30 (.node(write_en30));
  Pull_Resistor #(.pull(0)) pull_resistor_31 (.node(write_en31));
  Register #(.width(32), .trigger("rising"), .Select("low")) register_28 (
    .D(Write_Data), .en(write_en7), .Q(a3), .clk(clk));  // open: clr
  Register #(.width(32), .trigger("rising"), .Select("low")) register_29 (
    .D(Write_Data), .en(write_en15), .Q(t3), .clk(clk));  // open: clr
  Register #(.width(32), .trigger("rising"), .Select("low")) register_30 (
    .D(Write_Data), .en(write_en23), .Q(s0), .clk(clk));  // open: clr
  Register #(.width(32), .trigger("rising"), .Select("low")) register_31 (
    .D(Write_Data), .en(write_en31), .Q(s8), .clk(clk));  // open: clr
  // Probe on Read_Data_2
  Multiplexer #(.select(5), .width(32), .disabled("Z"), .enable("false")) multiplexer_2 (
    .in0({32{1'b0}}), .in1(ra), .in2(tp), .in3(sp), .in4(a0), .in5(a1), .in6(a2), .in7(a3), .in8(a4),
    .in9(a5), .in10(a6), .in11(a7), .in12(t0), .in13(t1), .in14(t2), .in15(t3), .in16(t4), .in17(t5),
    .in18(t6), .in19(t7), .in20(t8), .in21(u0), .in22(fp_s9), .in23(s0), .in24(s1), .in25(s2), .in26(s3),
    .in27(s4), .in28(s5), .in29(s6), .in30(s7), .in31(s8), .out(Read_Data_2), .sel(rs2));
  // Probe on rs2

  // Other names for the same wires on the sheet: read_data1[31:0] = Read_Data_1; read_data2[31:0] = Read_Data_2;
  //   read_reg1[4:0] = rs1; read_reg2[4:0] = rs2; write_en = RegWE; write_reg[4:0] = rd; x1[31:0] = ra; x2[31:0] = tp;
  //   x3[31:0] = sp; x4[31:0] = a0; x5[31:0] = a1; x6[31:0] = a2; x7[31:0] = a3; x8[31:0] = a4; x9[31:0] = a5;
  //   x10[31:0] = a6; x11[31:0] = a7; x12[31:0] = t0; x13[31:0] = t1; x14[31:0] = t2; x15[31:0] = t3; x16[31:0] = t4;
  //   x17[31:0] = t5; x18[31:0] = t6; x19[31:0] = t7; x20[31:0] = t8; x21[31:0] = u0; x22[31:0] = fp_s9;
  //   x23[31:0] = s0; x24[31:0] = s1; x25[31:0] = s2; x26[31:0] = s3; x27[31:0] = s4; x28[31:0] = s5; x29[31:0] = s6;
  //   x30[31:0] = s7; x31[31:0] = s8

  // Notes on the sheet:
  //   INPUTS to your circuit
  //   OUTPUTS from your circuit
  //   DON'T CHANGE THE LOCATIONS OF THE INPUTS AND OUTPUTS!
  //   These are DEBUG/TEST outputs from your circuit.
endmodule

module ImmModel (
  input  [2:0] ImmSel,
  input  [25:0] Imm_in,
  output [31:0] Imm_out
);

  wire [31:0] bit_extender_1_out, bit_extender_2_out, bit_extender_3_out, bit_extender_4_out,
       bit_extender_5_out;

  assign bit_extender_1_out = {{27{1'b0}}, Imm_in[14:10]};  // Bit_Extender bit_extender_1
  assign bit_extender_2_out = {{20{1'b0}}, Imm_in[21:10]};  // Bit_Extender bit_extender_2
  assign bit_extender_3_out = {{20{Imm_in[21]}}, Imm_in[21:10]};  // Bit_Extender bit_extender_3
  assign bit_extender_4_out = {{14{Imm_in[25]}}, {Imm_in[25:10], 2'b00}};  // Bit_Extender bit_extender_4
  assign bit_extender_5_out = {{4{Imm_in[9]}}, {Imm_in[9:0], Imm_in[25:10], 2'b00}};  // Bit_Extender bit_extender_5
  Multiplexer #(.select(3), .width(32), .disabled("Z"), .enable("false")) multiplexer_1 (
    .in0(bit_extender_1_out), .in1(bit_extender_2_out), .in2(bit_extender_3_out),
    .in3({Imm_in[24:5], {12{1'b0}}}), .in4(bit_extender_4_out), .in5(bit_extender_5_out), .out(Imm_out),
    .sel(ImmSel));  // open: in6, in7

  // Notes on the sheet:
  //   2RI5
  //   andi/ori/xori
  //   2RI12
  //   1RI20
  //   2RI16
  //   I26
endmodule

module AluModel (
  input  [31:0] A,
  input  [31:0] B,
  input  [3:0] ALUSel,
  output [31:0] Result
);

  wire adder_3_cout, bitselector_1_out, bitselector_2_out, xor_1_out;
  wire [0:0] slt_alu, sltu_alu;
  wire [31:0] add, adder_1_out, adder_3_out, and_alu, divu_alu, mul_alu, mulh_alu, mulhu_alu,
       multiplexer_1_out, multiplexer_2_out, multiplier_1_cout, multiplier_1_out, negator_1_out,
       negator_2_out, not_1_out, not_2_out, or_alu, remu_alu, sll_alu, sra_alu, srl_alu, sub_alu, xor_alu;

  BitSelector #(.width(32), .group(1)) bitselector_1 (.in(A), .out(bitselector_1_out), .sel({5{1'b1}}));
  BitSelector #(.width(32), .group(1)) bitselector_2 (.in(B), .out(bitselector_2_out), .sel({5{1'b1}}));
  Negator #(.width(32)) negator_1 (.in(A), .out(negator_1_out));
  Negator #(.width(32)) negator_2 (.in(B), .out(negator_2_out));
  Multiplexer #(.select(1), .width(32), .disabled("Z"), .enable("false")) multiplexer_1 (
    .in0(A), .in1(negator_1_out), .out(multiplexer_1_out), .sel(bitselector_1_out));
  Multiplexer #(.select(1), .width(32), .disabled("Z"), .enable("false")) multiplexer_2 (
    .in0(B), .in1(negator_2_out), .out(multiplexer_2_out), .sel(bitselector_2_out));
  Multiplier #(.width(32)) multiplier_1 (
    .a(multiplexer_1_out), .b(multiplexer_2_out), .out(multiplier_1_out), .cout(multiplier_1_cout));  // open: cin
  xor xor_1 (xor_1_out, bitselector_1_out, bitselector_2_out);
  assign not_1_out = ~multiplier_1_out;  // NOT_Gate not_1, 32 bits wide
  Adder #(.width(32)) adder_1 (.a({32{1'b0}}), .b(not_2_out), .out(adder_1_out), .cin(adder_3_cout));  // open: cout
  assign not_2_out = ~multiplier_1_cout;  // NOT_Gate not_2, 32 bits wide
  Adder #(.width(32)) adder_2 (.a(A), .b(B), .out(add));  // open: cin, cout
  assign and_alu = A & B;  // AND_Gate and_1, 32 bits wide
  assign or_alu = A | B;  // OR_Gate or_1, 32 bits wide
  assign xor_alu = A ^ B;  // XOR_Gate xor_2, 32 bits wide
  Shifter #(.width(32), .shift("lr")) shifter_1 (.in(A), .\dist (B[4:0]), .out(srl_alu));
  Shifter #(.width(32), .shift("ar")) shifter_2 (.in(A), .\dist (B[4:0]), .out(sra_alu));
  Shifter #(.width(32), .shift("ll")) shifter_3 (.in(A), .\dist (B[4:0]), .out(sll_alu));
  Adder #(.width(32)) adder_3 (.a(32'h1), .b(not_1_out), .out(adder_3_out), .cout(adder_3_cout));  // open: cin
  Multiplexer #(.select(1), .width(32), .disabled("Z"), .enable("false")) multiplexer_3 (
    .in0(multiplier_1_out), .in1(adder_3_out), .out(mul_alu), .sel(xor_1_out));
  Multiplexer #(.select(1), .width(32), .disabled("Z"), .enable("false")) multiplexer_4 (
    .in0(multiplier_1_cout), .in1(adder_1_out), .out(mulh_alu), .sel(xor_1_out));
  Comparator #(.width(32), .mode("twosComplement")) comparator_1 (.a(A), .b(B), .lt(slt_alu[0]));  // open: gt, eq
  Comparator #(.width(32), .mode("unsigned")) comparator_2 (.a(A), .b(B), .lt(sltu_alu[0]));  // open: gt, eq
  Divider #(.width(32)) divider_1 (.a(A), .b(B), .out(divu_alu), .rem(remu_alu));  // open: upper
  Multiplier #(.width(32)) multiplier_2 (.a(A), .b(B), .cout(mulhu_alu));  // open: out, cin
  Subtractor #(.width(32)) subtractor_1 (.a(A), .b(B), .out(sub_alu));  // open: bin, bout
  // Probe on Result
  Multiplexer #(.select(4), .width(32), .disabled("Z"), .enable("false")) multiplexer_5 (
    .in0(add), .in1(and_alu), .in2(or_alu), .in3(xor_alu), .in4(srl_alu), .in5(sra_alu), .in6(sll_alu),
    .in7({{31{1'b0}}, slt_alu[0]}), .in8(divu_alu), .in9(remu_alu), .in10(mul_alu), .in11(mulhu_alu),
    .in12(sub_alu), .in13(B), .in14(mulh_alu), .in15({{31{1'b0}}, sltu_alu[0]}), .out(Result), .sel(ALUSel));

  // Notes on the sheet:
  //   INPUTS to your circuit
  //   DON'T CHANGE THE LOCATIONS OF THE INPUTS AND OUTPUTS!
  //   OUTPUT from your circuit
endmodule

module Branch (
  input  [31:0] Rj,
  input  [31:0] Rd,
  input  BrUN,
  output BrEQ,
  output BrLT
);

  wire comparator_1_lt, comparator_2_lt;

  Comparator #(.width(32), .mode("twosComplement")) comparator_1 (
    .a(Rj), .b(Rd), .eq(BrEQ), .lt(comparator_1_lt));  // open: gt
  Comparator #(.width(32), .mode("unsigned")) comparator_2 (.a(Rj), .b(Rd), .lt(comparator_2_lt));  // open: gt, eq
  Multiplexer #(.select(1), .width(1), .disabled("Z"), .enable("false")) multiplexer_1 (
    .in0(comparator_1_lt), .in1(comparator_2_lt), .out(BrLT), .sel(BrUN));
endmodule

module IROM (
  input  [31:0] Program_counter,
  output [31:0] Instruction
);

  ROM #(.addrWidth(16), .dataWidth(32), .Select("high")) rom_1 (.addr(Program_counter[17:2]), .data(Instruction));
endmodule

module DRAM (
  input  [31:0] Write_Data,
  input  clk,
  input  Read_En,
  input  [31:0] Address,
  input  [3:0] Write_En,
  output [15:0] MissNubmer,
  output [31:0] Read_Data
);

  wire and_1_out, and_2_out, and_3_out, and_4_out, is_MemAddr, is_RomAddr, or_1_out, wreq;
  wire [15:0] controlled_buffer_3_out;
  wire [31:0] controlled_buffer_1_out, controlled_buffer_2_out, ram_data, rom_1_data, wdata_to_ram;

  Comparator #(.width(4), .mode("unsigned")) comparator_1 (
    .a(Address[31:28]), .b(4'b1000), .eq(is_RomAddr));  // open: gt, lt
  or or_1 (or_1_out, wreq, Read_En);
  not not_1 (is_MemAddr, is_RomAddr);
  and and_1 (and_1_out, or_1_out, is_MemAddr);
  assign controlled_buffer_1_out = and_1_out ? Address : 32'bz;  // Controlled_Buffer controlled_buffer_1
  assign controlled_buffer_2_out = and_2_out ? wdata_to_ram : 32'bz;  // Controlled_Buffer controlled_buffer_2
  and and_2 (and_2_out, wreq, is_MemAddr);
  assign controlled_buffer_3_out = is_RomAddr ? Address[17:2] : 16'bz;  // Controlled_Buffer controlled_buffer_3
  RAM #(.addrWidth(16), .dataWidth(32), .bus("separate"), .Select("high")) ram_1 (
    .addr(controlled_buffer_1_out[17:2]), .din(controlled_buffer_2_out), .data(ram_data), .str(and_2_out),
    .sel(1'b1), .clk(clk), .ld(1'b1));  // open: clr
  ROM #(.addrWidth(16), .dataWidth(32), .Select("high")) rom_1 (
    .addr(controlled_buffer_3_out), .data(rom_1_data), .sel(1'b1));
  or or_2 (wreq, Write_En[0], Write_En[1], Write_En[2], Write_En[3]);
  and and_3 (and_3_out, Read_En, is_MemAddr);
  assign Read_Data = and_3_out ? ram_data : 32'bz;  // Controlled_Buffer controlled_buffer_4
  assign Read_Data = and_4_out ? rom_1_data : 32'bz;  // Controlled_Buffer controlled_buffer_5
  and and_4 (and_4_out, Read_En, is_RomAddr);
  WrBorH wrborh_1 (.we(Write_En), .wdata_din(Write_Data), .ram_din(ram_data), .wdata_to_ram(wdata_to_ram));

  // Other names for the same wires on the sheet: Addr[31:0] = Address; MissNumber[15:0] = MissNubmer;
  //   ReadData[31:0] = Read_Data; ReadEnable = Read_En; rreq = Read_En; WriteData[31:0] = Write_Data;
  //   WriteEnable[3:0] = Write_En

  // Notes on the sheet:
  //   输入引脚区
  //   RAM
  //   二级存储器 ROM
  //   contents of rom_1 (hex, n*v repeats v):
  //   0 1 2 3 4 5 6 7 8 9 a b c d e f 10 11 12 13 14 15 16 17 18 19 1a 1b 1c 1d 1e 1f 20 21 22 23 24 25 26
  //   27 28 29 2a 2b 2c 2d 2e 2f 30 31 32 33 34 35 36 37 38 39 3a 3b 3c 3d 3e 3f 40 41 42 43 44 45 46 47
  //   48 49 4a 4b 4c 4d 4e 4f 50 51 52 53 54 55 56 57 58 59 5a 5b 5c 5d 5e 5f 60 61 62 63 64 65 66 67 68
  //   69 6a 6b 6c 6d 6e 6f 70 71 72 73 74 75 76 77 78 79 7a 7b 7c 7d 7e 7f ffffff80 ffffff81 ffffff82
  //   ffffff83 ffffff84 ffffff85 ffffff86 ffffff87 ffffff88 ffffff89 ffffff8a ffffff8b ffffff8c ffffff8d
  //   ffffff8e ffffff8f ffffff90 ffffff91 ffffff92 ffffff93 ffffff94 ffffff95 ffffff96 ffffff97 ffffff98
  //   ffffff99 ffffff9a ffffff9b ffffff9c ffffff9d ffffff9e ffffff9f ffffffa0 ffffffa1 ffffffa2 ffffffa3
  //   ffffffa4 ffffffa5 ffffffa6 ffffffa7 ffffffa8 ffffffa9 ffffffaa ffffffab ffffffac ffffffad ffffffae
  //   ffffffaf ffffffb0 ffffffb1 ffffffb2 ffffffb3 ffffffb4 ffffffb5 ffffffb6 ffffffb7 ffffffb8 ffffffb9
  //   ffffffba ffffffbb ffffffbc ffffffbd ffffffbe ffffffbf ffffffc0 ffffffc1 ffffffc2 ffffffc3 ffffffc4
  //   ffffffc5 ffffffc6 ffffffc7 ffffffc8 ffffffc9 ffffffca ffffffcb ffffffcc ffffffcd ffffffce ffffffcf
  //   ffffffd0 ffffffd1 ffffffd2 ffffffd3 ffffffd4 ffffffd5 ffffffd6 ffffffd7 ffffffd8 ffffffd9 ffffffda
  //   ffffffdb ffffffdc ffffffdd ffffffde ffffffdf ffffffe0 ffffffe1 ffffffe2 ffffffe3 ffffffe4 ffffffe5
  //   ffffffe6 ffffffe7 ffffffe8 ffffffe9 ffffffea ffffffeb ffffffec ffffffed ffffffee ffffffef fffffff0
  //   fffffff1 fffffff2 fffffff3 fffffff4 fffffff5 fffffff6 fffffff7 fffffff8 fffffff9 fffffffa fffffffb
  //   fffffffc fffffffd fffffffe ffffffff 0 1 2 3 4 5 6 7 8 9 a b c d e f 10 11 12 13 14 15 16 17 18 19 1a
  //   1b 1c 1d 1e 1f 20 21 22 23 24 25 26 27 28 29 2a 2b 2c 2d 2e 2f 30 31 32 33 34 35 36 37 38 39 3a 3b
  //   3c 3d 3e 3f 40 41 42 43 44 45 46 47 48 49 4a 4b 4c 4d 4e 4f 50 51 52 53 54 55 56 57 58 59 5a 5b 5c
  //   5d 5e 5f 60 61 62 63 64 65 66 67 68 69 6a 6b 6c 6d 6e 6f 70 71 72 73 74 75 76 77 78 79 7a 7b 7c 7d
  //   7e 7f ffffff80 ffffff81 ffffff82 ffffff83 ffffff84 ffffff85 ffffff86 ffffff87 ffffff88 ffffff89
  //   ffffff8a ffffff8b ffffff8c ffffff8d ffffff8e ffffff8f ffffff90 ffffff91 ffffff92 ffffff93 ffffff94
  //   ffffff95 ffffff96 ffffff97 ffffff98 ffffff99 ffffff9a ffffff9b ffffff9c ffffff9d ffffff9e ffffff9f
  //   ffffffa0 ffffffa1 ffffffa2 ffffffa3 ffffffa4 ffffffa5 ffffffa6 ffffffa7 ffffffa8 ffffffa9 ffffffaa
  //   ffffffab ffffffac ffffffad ffffffae ffffffaf ffffffb0 ffffffb1 ffffffb2 ffffffb3 ffffffb4 ffffffb5
  //   ffffffb6 ffffffb7 ffffffb8 ffffffb9 ffffffba ffffffbb ffffffbc ffffffbd ffffffbe ffffffbf ffffffc0
  //   ffffffc1 ffffffc2 ffffffc3 ffffffc4 ffffffc5 ffffffc6 ffffffc7 ffffffc8 ffffffc9 ffffffca ffffffcb
  //   ffffffcc ffffffcd ffffffce ffffffcf ffffffd0 ffffffd1 ffffffd2 ffffffd3 ffffffd4 ffffffd5 ffffffd6
  //   ffffffd7 ffffffd8 ffffffd9 ffffffda ffffffdb ffffffdc ffffffdd ffffffde ffffffdf ffffffe0 ffffffe1
  //   ffffffe2 ffffffe3 ffffffe4 ffffffe5 ffffffe6 ffffffe7 ffffffe8 ffffffe9 ffffffea ffffffeb ffffffec
  //   ffffffed ffffffee ffffffef fffffff0 fffffff1 fffffff2 fffffff3 fffffff4 fffffff5 fffffff6 fffffff7
  //   fffffff8 fffffff9 fffffffa fffffffb fffffffc fffffffd fffffffe ffffffff 0 1 2 3 4 5 6 7 8 9 a b c d
  //   e f 10 11 12 13 14 15 16 17 18 19 1a 1b 1c 1d 1e 1f 20 21 22 23 24 25 26 27 28 29 2a 2b 2c 2d 2e 2f
  //   30 31 32 33 34 35 36 37 38 39 3a 3b 3c 3d 3e 3f 40 41 42 43 44 45 46 47 48 49 4a 4b 4c 4d 4e 4f 50
  //   51 52 53 54 55 56 57 58 59 5a 5b 5c 5d 5e 5f 60 61 62 63 64 65 66 67 68 69 6a 6b 6c 6d 6e 6f 70 71
  //   72 73 74 75 76 77 78 79 7a 7b 7c 7d 7e 7f ffffff80 ffffff81 ffffff82 ffffff83 ffffff84 ffffff85
  //   ffffff86 ffffff87 ffffff88 ffffff89 ffffff8a ffffff8b ffffff8c ffffff8d ffffff8e ffffff8f ffffff90
  //   ffffff91 ffffff92 ffffff93 ffffff94 ffffff95 ffffff96 ffffff97 ffffff98 ffffff99 ffffff9a ffffff9b
  //   ffffff9c ffffff9d ffffff9e ffffff9f ffffffa0 ffffffa1 ffffffa2 ffffffa3 ffffffa4 ffffffa5 ffffffa6
  //   ffffffa7 ffffffa8 ffffffa9 ffffffaa ffffffab ffffffac ffffffad ffffffae ffffffaf ffffffb0 ffffffb1
  //   ffffffb2 ffffffb3 ffffffb4 ffffffb5 ffffffb6 ffffffb7 ffffffb8 ffffffb9 ffffffba ffffffbb ffffffbc
  //   ffffffbd ffffffbe ffffffbf ffffffc0 ffffffc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
  //   输出引脚区
endmodule

module WrBorH (
  input  [3:0] we,
  input  [31:0] wdata_din,
  input  [31:0] ram_din,
  output [31:0] wdata_to_ram
);

  wire wr_b0, wr_b1, wr_b2, wr_b3, wr_h0, wr_h1, wr_w;
  wire [31:0] and_1_out, and_2_out, and_3_out, and_4_out, and_5_out, and_6_out, and_7_out, and_8_out,
       controlled_buffer_1_out, or_1_out, shifter_1_out, shifter_2_out, shifter_3_out, shifter_4_out,
       wdata_from_cpu;

  Comparator #(.width(4), .mode("unsigned")) comparator_1 (.a(we), .b(4'b0001), .eq(wr_b0));  // open: gt, lt
  Comparator #(.width(4), .mode("unsigned")) comparator_2 (.a(we), .b(4'b0010), .eq(wr_b1));  // open: gt, lt
  Comparator #(.width(4), .mode("unsigned")) comparator_3 (.a(we), .b(4'b0100), .eq(wr_b2));  // open: gt, lt
  Comparator #(.width(4), .mode("unsigned")) comparator_4 (.a(we), .b(4'b1000), .eq(wr_b3));  // open: gt, lt
  Comparator #(.width(4), .mode("unsigned")) comparator_5 (.a(we), .b(4'b0011), .eq(wr_h0));  // open: gt, lt
  Comparator #(.width(4), .mode("unsigned")) comparator_6 (.a(we), .b(4'b1100), .eq(wr_h1));  // open: gt, lt
  Comparator #(.width(4), .mode("unsigned")) comparator_7 (.a(we), .b(4'b1111), .eq(wr_w));  // open: gt, lt
  assign and_1_out = wdata_din & 32'hff;  // AND_Gate and_1, 32 bits wide
  assign and_2_out = wdata_din & 32'hffff;  // AND_Gate and_2, 32 bits wide
  assign and_3_out = ram_din & 32'hffffff00;  // AND_Gate and_3, 32 bits wide
  assign and_4_out = ram_din & 32'hffff00ff;  // AND_Gate and_4, 32 bits wide
  assign and_5_out = ram_din & 32'hff00ffff;  // AND_Gate and_5, 32 bits wide
  assign and_6_out = ram_din & 32'hffffff;  // AND_Gate and_6, 32 bits wide
  assign and_7_out = ram_din & 32'hffff0000;  // AND_Gate and_7, 32 bits wide
  assign and_8_out = ram_din & 32'hffff;  // AND_Gate and_8, 32 bits wide
  Shifter #(.width(32), .shift("ll")) shifter_1 (.in(and_1_out), .\dist (5'b01000), .out(shifter_1_out));
  Shifter #(.width(32), .shift("ll")) shifter_2 (.in(and_1_out), .\dist (5'b10000), .out(shifter_2_out));
  Shifter #(.width(32), .shift("ll")) shifter_3 (.in(and_1_out), .\dist (5'b11000), .out(shifter_3_out));
  Shifter #(.width(32), .shift("ll")) shifter_4 (.in(and_2_out), .\dist (5'b10000), .out(shifter_4_out));
  assign controlled_buffer_1_out = wr_b0 ? and_3_out : 32'bz;  // Controlled_Buffer controlled_buffer_1
  assign controlled_buffer_1_out = wr_b1 ? and_4_out : 32'bz;  // Controlled_Buffer controlled_buffer_2
  assign controlled_buffer_1_out = wr_b2 ? and_5_out : 32'bz;  // Controlled_Buffer controlled_buffer_3
  assign controlled_buffer_1_out = wr_b3 ? and_6_out : 32'bz;  // Controlled_Buffer controlled_buffer_4
  assign controlled_buffer_1_out = wr_h0 ? and_7_out : 32'bz;  // Controlled_Buffer controlled_buffer_5
  assign controlled_buffer_1_out = wr_h1 ? and_8_out : 32'bz;  // Controlled_Buffer controlled_buffer_6
  assign wdata_from_cpu = wr_b0 ? and_1_out : 32'bz;  // Controlled_Buffer controlled_buffer_7
  assign wdata_from_cpu = wr_b1 ? shifter_1_out : 32'bz;  // Controlled_Buffer controlled_buffer_8
  assign wdata_from_cpu = wr_b2 ? shifter_2_out : 32'bz;  // Controlled_Buffer controlled_buffer_9
  assign wdata_from_cpu = wr_b3 ? shifter_3_out : 32'bz;  // Controlled_Buffer controlled_buffer_10
  assign wdata_from_cpu = wr_h0 ? and_2_out : 32'bz;  // Controlled_Buffer controlled_buffer_11
  assign wdata_from_cpu = wr_h1 ? shifter_4_out : 32'bz;  // Controlled_Buffer controlled_buffer_12
  assign wdata_from_cpu = wr_w ? wdata_din : 32'bz;  // Controlled_Buffer controlled_buffer_13
  assign or_1_out = controlled_buffer_1_out | wdata_from_cpu;  // OR_Gate or_1, 32 bits wide
  Multiplexer #(.select(1), .width(32), .disabled("Z"), .enable("false")) multiplexer_1 (
    .in0(or_1_out), .in1(wdata_from_cpu), .out(wdata_to_ram), .sel(wr_w));
endmodule

module W2BorH (
  input  [31:0] din,
  input  \signed ,
  input  [3:0] mask,
  output [31:0] dout
);

  wire comparator_1_eq, comparator_2_eq, comparator_3_eq, comparator_4_eq, comparator_5_eq, comparator_6_eq,
       comparator_7_eq;
  wire [31:0] and_1_out, and_2_out, and_3_out, and_5_out, byte0, byte0_sext, byte0_uext, byte1, byte1_sext,
       byte1_uext, byte2, byte2_sext, byte2_uext, byte3, byte3_sext, byte3_uext, halfw0, halfw0_sext,
       halfw0_uext, halfw1, halfw1_sext, halfw1_uext;

  assign and_1_out = din & 32'hff;  // AND_Gate and_1, 32 bits wide
  assign and_2_out = din & 32'hff00;  // AND_Gate and_2, 32 bits wide
  assign and_3_out = din & 32'hff0000;  // AND_Gate and_3, 32 bits wide
  assign byte3 = din & 32'hff000000;  // AND_Gate and_4, 32 bits wide
  assign and_5_out = din & 32'hffff;  // AND_Gate and_5, 32 bits wide
  assign halfw1 = din & 32'hffff0000;  // AND_Gate and_6, 32 bits wide
  Comparator #(.width(4), .mode("unsigned")) comparator_1 (
    .a(mask), .b(4'b0001), .eq(comparator_1_eq));  // open: gt, lt
  Comparator #(.width(4), .mode("unsigned")) comparator_2 (
    .a(mask), .b(4'b0010), .eq(comparator_2_eq));  // open: gt, lt
  Comparator #(.width(4), .mode("unsigned")) comparator_3 (
    .a(mask), .b(4'b0100), .eq(comparator_3_eq));  // open: gt, lt
  Comparator #(.width(4), .mode("unsigned")) comparator_4 (
    .a(mask), .b(4'b1000), .eq(comparator_4_eq));  // open: gt, lt
  Comparator #(.width(4), .mode("unsigned")) comparator_5 (
    .a(mask), .b(4'b0011), .eq(comparator_5_eq));  // open: gt, lt
  Comparator #(.width(4), .mode("unsigned")) comparator_6 (
    .a(mask), .b(4'b1100), .eq(comparator_6_eq));  // open: gt, lt
  Comparator #(.width(4), .mode("unsigned")) comparator_7 (
    .a(mask), .b(4'b1111), .eq(comparator_7_eq));  // open: gt, lt
  Shifter #(.width(32), .shift("ll")) shifter_1 (.in(and_1_out), .\dist (5'b11000), .out(byte0));
  Shifter #(.width(32), .shift("ll")) shifter_2 (.in(and_2_out), .\dist (5'b10000), .out(byte1));
  Shifter #(.width(32), .shift("ll")) shifter_3 (.in(and_3_out), .\dist (5'b01000), .out(byte2));
  Shifter #(.width(32), .shift("ll")) shifter_4 (.in(and_5_out), .\dist (5'b10000), .out(halfw0));
  Multiplexer #(.select(1), .width(32), .disabled("Z"), .enable("true")) multiplexer_1 (
    .in0(byte0_uext), .in1(byte0_sext), .out(dout), .sel(\signed ), .en(comparator_1_eq));
  Multiplexer #(.select(1), .width(32), .disabled("Z"), .enable("true")) multiplexer_2 (
    .in0(byte1_uext), .in1(byte1_sext), .out(dout), .sel(\signed ), .en(comparator_2_eq));
  Multiplexer #(.select(1), .width(32), .disabled("Z"), .enable("true")) multiplexer_3 (
    .in0(byte2_uext), .in1(byte2_sext), .out(dout), .sel(\signed ), .en(comparator_3_eq));
  Multiplexer #(.select(1), .width(32), .disabled("Z"), .enable("true")) multiplexer_4 (
    .in0(byte3_uext), .in1(byte3_sext), .out(dout), .sel(\signed ), .en(comparator_4_eq));
  Multiplexer #(.select(1), .width(32), .disabled("Z"), .enable("true")) multiplexer_5 (
    .in0(halfw0_uext), .in1(halfw0_sext), .out(dout), .sel(\signed ), .en(comparator_5_eq));
  Multiplexer #(.select(1), .width(32), .disabled("Z"), .enable("true")) multiplexer_6 (
    .in0(halfw1_uext), .in1(halfw1_sext), .out(dout), .sel(\signed ), .en(comparator_6_eq));
  assign dout = comparator_7_eq ? din : 32'bz;  // Controlled_Buffer controlled_buffer_1
  Shifter #(.width(32), .shift("lr")) shifter_5 (.in(byte0), .\dist (5'b11000), .out(byte0_uext));
  Shifter #(.width(32), .shift("ar")) shifter_6 (.in(byte0), .\dist (5'b11000), .out(byte0_sext));
  Shifter #(.width(32), .shift("lr")) shifter_7 (.in(byte1), .\dist (5'b11000), .out(byte1_uext));
  Shifter #(.width(32), .shift("ar")) shifter_8 (.in(byte1), .\dist (5'b11000), .out(byte1_sext));
  Shifter #(.width(32), .shift("lr")) shifter_9 (.in(byte2), .\dist (5'b11000), .out(byte2_uext));
  Shifter #(.width(32), .shift("ar")) shifter_10 (.in(byte2), .\dist (5'b11000), .out(byte2_sext));
  Shifter #(.width(32), .shift("lr")) shifter_11 (.in(byte3), .\dist (5'b11000), .out(byte3_uext));
  Shifter #(.width(32), .shift("ar")) shifter_12 (.in(byte3), .\dist (5'b11000), .out(byte3_sext));
  Shifter #(.width(32), .shift("lr")) shifter_13 (.in(halfw0), .\dist (5'b10000), .out(halfw0_uext));
  Shifter #(.width(32), .shift("ar")) shifter_14 (.in(halfw0), .\dist (5'b10000), .out(halfw0_sext));
  Shifter #(.width(32), .shift("lr")) shifter_15 (.in(halfw1), .\dist (5'b10000), .out(halfw1_uext));
  Shifter #(.width(32), .shift("ar")) shifter_16 (.in(halfw1), .\dist (5'b10000), .out(halfw1_sext));

  // Other names for the same wires on the sheet: sign = \signed ; word[31:0] = din
endmodule

module IOBus (
  input  [31:0] WriteAddr,
  input  [31:0] WriteData,
  input  R,
  input  [3:0] W,
  input  [31:0] IOReadData,
  input  [31:0] MemRead,
  output [31:0] ReadData,
  output [3:0] out_8,
  output IOEn,
  output [11:0] IOAddr12,
  output [31:0] IOWriteData,
  output [31:0] MemAddr,
  output MemR,
  output [3:0] MemW,
  output [31:0] MemWriteData
);

  wire and_2_out, and_3_out, and_4_out, and_5_out, is_MemAddr, is_PeriAddr, or_2_out, or_3_out, wreq;
  wire [3:0] controlled_buffer_4_out;

  // Probe on WriteAddr
  assign MemW = is_MemAddr ? W : 4'bz;  // Controlled_Buffer controlled_buffer_1
  or or_1 (wreq, W[0], W[1], W[2], W[3]);
  Comparator #(.width(20), .mode("unsigned")) comparator_1 (
    .a(WriteAddr[31:12]), .b({20{1'b1}}), .eq(is_PeriAddr));  // open: gt, lt
  assign MemR = is_MemAddr ? R : 1'bz;  // Controlled_Buffer controlled_buffer_2
  // Probe on is_PeriAddr
  not not_1 (is_MemAddr, is_PeriAddr);
  and and_1 (IOEn, is_PeriAddr, or_2_out);
  or or_2 (or_2_out, wreq, R);
  or or_3 (or_3_out, wreq, R);
  and and_2 (and_2_out, is_MemAddr, or_3_out);
  // Probe on WriteAddr
  assign MemAddr = and_2_out ? WriteAddr : 32'bz;  // Controlled_Buffer controlled_buffer_3
  // Probe on MemAddr
  assign controlled_buffer_4_out = wreq ? W : 4'bz;  // Controlled_Buffer controlled_buffer_4
  assign out_8 = is_PeriAddr ? controlled_buffer_4_out : 4'bz;  // Controlled_Buffer controlled_buffer_5
  and and_3 (and_3_out, is_MemAddr, wreq);
  assign MemWriteData = and_3_out ? WriteData : 32'bz;  // Controlled_Buffer controlled_buffer_6
  Pull_Resistor #(.pull(0)) pull_resistor_1 (.node(out_8));
  and and_4 (and_4_out, R, IOEn);
  assign ReadData = and_4_out ? IOReadData : 32'bz;  // Controlled_Buffer controlled_buffer_7
  assign ReadData = and_5_out ? MemRead : 32'bz;  // Controlled_Buffer controlled_buffer_8
  and and_5 (and_5_out, R, is_MemAddr);
  // Probe on ReadData

  assign IOAddr12 = WriteAddr[11:0];
  assign IOWriteData = WriteData;

  // Other names for the same wires on the sheet: IOWe[3:0] = out_8; rreq = R
endmodule

module DigitDriver (
  input  in_1,
  input  IOEn,
  input  [31:0] IOWriteData,
  input  [3:0] IOWe,
  input  [11:0] IOAddr12,
  output [3:0] D0,
  output [3:0] D4,
  output [3:0] D1,
  output [3:0] D5,
  output [3:0] D2,
  output [3:0] D6,
  output [3:0] D3,
  output [3:0] D7
);

  wire and_1_out, comparator_1_eq;
  wire [31:0] controlled_buffer_1_out, wd2LED;

  Comparator #(.width(10), .mode("unsigned")) comparator_1 (
    .a({10{1'b0}}), .b(IOAddr12[11:2]), .eq(comparator_1_eq));  // open: gt, lt
  // Probe on IOEn
  // Probe on and_1_out
  and and_1 (and_1_out, comparator_1_eq, IOEn);
  // Probe on {D7, D6, D5, D4, D3, D2, D1, D0}
  WrBorH wrborh_1 (
    .we(IOWe), .wdata_din(IOWriteData), .ram_din({D7, D6, D5, D4, D3, D2, D1, D0}), .wdata_to_ram(wd2LED));
  // Probe on wd2LED
  assign controlled_buffer_1_out = and_1_out ? wd2LED : 32'bz;  // Controlled_Buffer controlled_buffer_1
  // Probe on controlled_buffer_1_out[3:0]
  // Probe on D0
  Register #(.width(4), .trigger("rising"), .Select("low")) register_1 (
    .D(controlled_buffer_1_out[3:0]), .en(and_1_out), .Q(D0), .clk(in_1));  // open: clr
  Register #(.width(4), .trigger("rising"), .Select("low")) register_2 (
    .D(controlled_buffer_1_out[7:4]), .en(and_1_out), .Q(D1), .clk(in_1));  // open: clr
  Register #(.width(4), .trigger("rising"), .Select("low")) register_3 (
    .D(controlled_buffer_1_out[11:8]), .en(and_1_out), .Q(D2), .clk(in_1));  // open: clr
  Register #(.width(4), .trigger("rising"), .Select("low")) register_4 (
    .D(controlled_buffer_1_out[15:12]), .en(and_1_out), .Q(D3), .clk(in_1));  // open: clr
  Register #(.width(4), .trigger("rising"), .Select("low")) register_5 (
    .D(controlled_buffer_1_out[19:16]), .en(and_1_out), .Q(D4), .clk(in_1));  // open: clr
  Register #(.width(4), .trigger("rising"), .Select("low")) register_6 (
    .D(controlled_buffer_1_out[23:20]), .en(and_1_out), .Q(D5), .clk(in_1));  // open: clr
  Register #(.width(4), .trigger("rising"), .Select("low")) register_7 (
    .D(controlled_buffer_1_out[27:24]), .en(and_1_out), .Q(D6), .clk(in_1));  // open: clr
  Register #(.width(4), .trigger("rising"), .Select("low")) register_8 (
    .D(controlled_buffer_1_out[31:28]), .en(and_1_out), .Q(D7), .clk(in_1));  // open: clr

  // Other names for the same wires on the sheet: clk = in_1; IOBase[9:0] = IOAddr12[11:2];
  //   LEDdata[31:0] = {D7, D6, D5, D4, D3, D2, D1, D0}; We[3:0] = IOWe

  // Notes on the sheet:
  //   输入管脚
  //   输出管脚
endmodule

module LEDDriver (
  input  in_1,
  input  IOEn,
  input  [31:0] IOWriteData,
  input  [3:0] IOWe,
  input  [11:0] IOAddr12,
  output [23:0] LED0
);

  wire and_1_out, comparator_1_eq;
  wire [23:0] controlled_buffer_1_out;
  wire [31:0] wd2LED;

  Comparator #(.width(10), .mode("unsigned")) comparator_1 (
    .a(10'h18), .b(IOAddr12[11:2]), .eq(comparator_1_eq));  // open: gt, lt
  // Probe on IOEn
  // Probe on and_1_out
  and and_1 (and_1_out, comparator_1_eq, IOEn);
  WrBorH wrborh_1 (.we(IOWe), .wdata_din(IOWriteData), .ram_din({{8{1'b0}}, LED0}), .wdata_to_ram(wd2LED));
  assign controlled_buffer_1_out = and_1_out ? wd2LED[23:0] : 24'bz;  // Controlled_Buffer controlled_buffer_1
  // Probe on controlled_buffer_1_out
  Register #(.width(24), .trigger("rising"), .Select("low")) register_1 (
    .D(controlled_buffer_1_out), .en(and_1_out), .Q(LED0), .clk(in_1));  // open: clr

  // Other names for the same wires on the sheet: clk = in_1; IOBase[9:0] = IOAddr12[11:2]; We[3:0] = IOWe

  // Notes on the sheet:
  //   输入管脚
  //   输出管脚
endmodule

module SwitchDriver (
  input  in_1,
  input  [23:0] SW0,
  input  IOEn,
  input  [11:0] IOAddr12,
  output [31:0] IOReadData
);

  wire and_1_out, comparator_1_eq;
  wire [31:0] multiplexer_1_out;

  Comparator #(.width(10), .mode("unsigned")) comparator_1 (
    .a(10'h1c), .b(IOAddr12[11:2]), .eq(comparator_1_eq));  // open: gt, lt
  and and_1 (and_1_out, comparator_1_eq, IOEn);
  Multiplexer #(.select(1), .width(32), .disabled("Z"), .enable("false")) multiplexer_1 (
    .in1({{8{1'b0}}, SW0}), .out(multiplexer_1_out), .sel(and_1_out));  // open: in0
  assign IOReadData = and_1_out ? multiplexer_1_out : 32'bz;  // Controlled_Buffer controlled_buffer_1

  // Other names for the same wires on the sheet: clk = in_1; IOBase[9:0] = IOAddr12[11:2]

  // Notes on the sheet:
  //   输入管脚
  //   输出管脚
endmodule

module Timer (
  input  in_1,
  input  IOEn,
  input  [31:0] IOWriteData,
  input  [3:0] IOWe,
  input  [11:0] IOAddr12,
  output [31:0] IOReadData
);

  wire and_1_out, and_2_out, and_3_out, comparator_1_eq, comparator_2_eq, threshold_reached, We;
  wire [31:0] counter_1_q, register_1_q, timer_q;

  Comparator #(.width(10), .mode("unsigned")) comparator_1 (
    .a(10'h8), .b(IOAddr12[11:2]), .eq(comparator_1_eq));  // open: gt, lt
  Comparator #(.width(10), .mode("unsigned")) comparator_2 (
    .a(10'h9), .b(IOAddr12[11:2]), .eq(comparator_2_eq));  // open: gt, lt
  and and_1 (and_1_out, We, comparator_2_eq, IOEn);
  and and_2 (and_2_out, comparator_1_eq, IOEn);
  Register #(.width(32), .trigger("rising"), .Select("low")) register_1 (
    .D(IOWriteData), .en(and_1_out), .Q(register_1_q), .clk(in_1));  // open: clr
  Counter #(.width(32), .max('hffffffff), .ongoal("wrap"), .trigger("rising"), .behavior("new")) counter_1 (
    .load(threshold_reached), .D({32{1'b0}}), .Q(counter_1_q), .clk(in_1));  // open: count, carry, clr, preset, down
  and and_3 (and_3_out, We, and_2_out);
  or or_1 (We, IOWe[0], IOWe[1], IOWe[2], IOWe[3]);
  Comparator #(.width(32), .mode("unsigned")) comparator_3 (
    .a(register_1_q), .b(counter_1_q), .eq(threshold_reached));  // open: gt, lt
  Counter #(.width(32), .max('hffffffff), .ongoal("wrap"), .trigger("rising"), .behavior("new")) timer (
    .load(and_3_out), .D(IOWriteData), .count(threshold_reached), .Q(timer_q), .clk(in_1));  // open: carry, clr, preset, down
  assign IOReadData = and_2_out ? timer_q : 32'bz;  // Controlled_Buffer controlled_buffer_1

  // Other names for the same wires on the sheet: clk = in_1; IOBase[9:0] = IOAddr12[11:2]; timer[31:0] = IOReadData

  // Notes on the sheet:
  //   输入管脚
  //   输出管脚
endmodule

module debug (
  input  [31:0] PC,
  input  [31:0] brkPC,
  input  clr,
  input  clk_i,
  output clk_o
);

  wire and_1_out, comparator_1_eq;

  Comparator #(.width(32), .mode("twosComplement")) comparator_1 (
    .a(PC), .b(brkPC), .eq(comparator_1_eq));  // open: gt, lt
  Pull_Resistor #(.pull(0)) pull_resistor_1 (.node(clr));
  and and_1 (and_1_out, comparator_1_eq, ~clr);  // AND_Gate
  and and_2 (clk_o, ~and_1_out, clk_i);  // AND_Gate
endmodule
