// Logisim project RISC-V_SoC.circ as structural Verilog: 18 circuits, main circuit SoC
module SoC (
);

  wire button_out, clk, continue_out, cpu_1_out_6, debug_1_clk_o, halt, iobus_1_ioen, iobus_1_memr;
  wire [3:0] cpu_1_out_7, digitdriver_1_d0, digitdriver_1_d1, digitdriver_1_d2, digitdriver_1_d3,
       digitdriver_1_d4, digitdriver_1_d5, digitdriver_1_d6, digitdriver_1_d7, iobus_1_iowe, iobus_1_memw;
  wire [11:0] iobus_1_ioaddr12;
  wire [15:0] MissNumber;
  wire [23:0] leddriver_1_led0, undriven;
  wire [31:0] cpu_1_out_17, cpu_1_out_18, cpu_1_out_19, dram_1_read_data, iobus_1_iowritedata,
       iobus_1_memaddr, iobus_1_memwritedata, iobus_1_readdata, irom_1_instruction, switchdriver_1_ioreaddata;

  Hex_Digit_Display hex_digit_display_1 (.value(digitdriver_1_d7));  // open: dp
  Hex_Digit_Display hex_digit_display_2 (.value(digitdriver_1_d6));  // open: dp
  Hex_Digit_Display hex_digit_display_3 (.value(digitdriver_1_d5));  // open: dp
  Clock #(.highDuration(1), .lowDuration(1)) clock_1 (.out(clk));
  Hex_Digit_Display hex_digit_display_4 (.value(digitdriver_1_d3));  // open: dp
  Hex_Digit_Display hex_digit_display_5 (.value(digitdriver_1_d4));  // open: dp
  Hex_Digit_Display hex_digit_display_6 (.value(digitdriver_1_d2));  // open: dp
  Hex_Digit_Display hex_digit_display_7 (.value(digitdriver_1_d1));  // open: dp
  DigitDriver digitdriver_1 (
    .in_1(clk), .IOEn(iobus_1_ioen), .IOWriteData(iobus_1_iowritedata), .IOAddr12(iobus_1_ioaddr12),
    .D0(digitdriver_1_d0), .D4(digitdriver_1_d4), .D1(digitdriver_1_d1), .D5(digitdriver_1_d5),
    .D2(digitdriver_1_d2), .D6(digitdriver_1_d6), .D3(digitdriver_1_d3), .D7(digitdriver_1_d7),
    .IOWe(iobus_1_iowe));
  IROM irom_1 (.Program_counter(cpu_1_out_17), .Instruction(irom_1_instruction));
  Hex_Digit_Display hex_digit_display_8 (.value(digitdriver_1_d0));  // open: dp
  // Probe on cpu_1_out_17
  // Probe on irom_1_instruction
  Button \continue  (.out(continue_out));
  LED #(.active("true")) _23 (.in(leddriver_1_led0[23]));
  LED #(.active("true")) _21 (.in(leddriver_1_led0[21]));
  LED #(.active("true")) _22 (.in(leddriver_1_led0[22]));
  debug debug_1 (.PC(cpu_1_out_17), .brkPC(32'h1c090000), .clr(continue_out), .clk_i(clk), .clk_o(debug_1_clk_o));
  LED #(.active("true")) _18 (.in(leddriver_1_led0[18]));
  LED #(.active("true")) _19 (.in(leddriver_1_led0[19]));
  LED #(.active("true")) _20 (.in(leddriver_1_led0[20]));
  LED #(.active("true")) _17 (.in(leddriver_1_led0[17]));
  LEDDriver leddriver_1 (
    .in_1(clk), .IOEn(iobus_1_ioen), .IOWriteData(iobus_1_iowritedata), .IOAddr12(iobus_1_ioaddr12),
    .LED0(leddriver_1_led0), .IOWe(iobus_1_iowe));
  LED #(.active("true")) _16 (.in(leddriver_1_led0[16]));
  LED #(.active("true")) _14 (.in(leddriver_1_led0[14]));
  LED #(.active("true")) _15 (.in(leddriver_1_led0[15]));
  LED #(.active("true")) _13 (.in(leddriver_1_led0[13]));
  LED #(.active("true")) _12 (.in(leddriver_1_led0[12]));
  LED #(.active("true")) _9 (.in(leddriver_1_led0[9]));
  LED #(.active("true")) _11 (.in(leddriver_1_led0[11]));
  LED #(.active("true")) _10 (.in(leddriver_1_led0[10]));
  Button button (.out(button_out));
  LED #(.active("true")) _5 (.in(leddriver_1_led0[5]));
  LED #(.active("true")) _6 (.in(leddriver_1_led0[6]));
  LED #(.active("true")) _8 (.in(leddriver_1_led0[8]));
  LED #(.active("true")) _7 (.in(leddriver_1_led0[7]));
  CPU cpu_1 (
    .in_3(debug_1_clk_o), .in_1(irom_1_instruction), .out_17(cpu_1_out_17), .out_18(cpu_1_out_18),
    .out_19(cpu_1_out_19), .out_6(cpu_1_out_6), .in_2(iobus_1_readdata), .out_7(cpu_1_out_7), .out_8(halt),
    .in_5(button_out));  // open: out_13, out_16, out_10, out_9, out_15, out_12, out_14, out_11, in_4
  LED #(.active("true")) _2 (.in(leddriver_1_led0[2]));
  LED #(.active("true")) _4 (.in(leddriver_1_led0[4]));
  LED #(.active("true")) _1 (.in(leddriver_1_led0[1]));
  LED #(.active("true")) _3 (.in(leddriver_1_led0[3]));
  LED #(.active("true")) _0 (.in(leddriver_1_led0[0]));
  // DipSwitch #(.NSwitches(24)) dipswitch_1: pin names not known; wires that end beside it: undriven[23], undriven[22], undriven[21], undriven[20], undriven[19], undriven[18], undriven[17], undriven[16], undriven[15], undriven[14], undriven[13], undriven[12]
  IOBus iobus_1 (
    .ReadData(iobus_1_readdata), .IOAddr12(iobus_1_ioaddr12), .IOEn(iobus_1_ioen), .R(cpu_1_out_6),
    .WriteAddr(cpu_1_out_18), .IOReadData(switchdriver_1_ioreaddata), .WriteData(cpu_1_out_19),
    .MemRead(dram_1_read_data), .IOWriteData(iobus_1_iowritedata), .MemAddr(iobus_1_memaddr),
    .MemR(iobus_1_memr), .MemWriteData(iobus_1_memwritedata), .W(cpu_1_out_7), .MemW(iobus_1_memw),
    .IOWe(iobus_1_iowe));
  SwitchDriver switchdriver_1 (
    .in_1(clk), .SW0(undriven), .IOEn(iobus_1_ioen), .IOAddr12(iobus_1_ioaddr12),
    .IOReadData(switchdriver_1_ioreaddata));
  DRAM dram_1 (
    .Write_En(iobus_1_memw), .clk(clk), .Read_Data(dram_1_read_data), .Address(iobus_1_memaddr),
    .Write_Data(iobus_1_memwritedata), .Read_En(iobus_1_memr), .MissNubmer(MissNumber));
  Timer timer_1 (
    .in_1(clk), .IOAddr12(iobus_1_ioaddr12), .IOReadData(switchdriver_1_ioreaddata),
    .IOWriteData(iobus_1_iowritedata), .IOEn(iobus_1_ioen), .IOWe(iobus_1_iowe));

  // Notes on the sheet:
  //   DK7
  //   DK5
  //   DK6
  //   DK4
  //   DK3
  //   时钟
  //   DK2
  //   DK1
  //   DK0
  //   23
  //   I/O总线
  //   22
  //   20
  //   19
  //   21
  //   18
  //   15
  //   16
  //   17
  //   14
  //   11
  //   12
  //   13
  //   9
  //   10
  //   8
  //   7
  //   5
  //   6
  //   3
  //   4
  //   0
  //   1
  //   2
endmodule

module CPU (
  input  [31:0] in_1,
  input  [31:0] in_2,
  input  in_3,
  input  in_4,
  input  in_5,
  output out_6,
  output [3:0] out_7,
  output out_8,
  output [31:0] out_9,
  output [31:0] out_10,
  output [31:0] out_11,
  output [31:0] out_12,
  output [31:0] out_13,
  output [31:0] out_14,
  output [31:0] out_15,
  output [31:0] out_16,
  output [31:0] out_17,
  output [31:0] out_18,
  output [31:0] out_19
);

  wire and_2_out, and_3_out, and_4_out, and_5_out, branch_1_breq, branch_1_brlt, controlmodel_1_alusela,
       controlmodel_1_aluselb, controlmodel_1_beq, controlmodel_1_bge, controlmodel_1_bgeu,
       controlmodel_1_blt, controlmodel_1_bltu, controlmodel_1_bne, controlmodel_1_brun, controlmodel_1_jmp,
       controlmodel_1_regwrite, En, exc, intr1, load_sign, mie, or_1_out, or_2_out, or_3_out, PCSel, trapRet,
       Zicsr;
  wire [1:0] controlmodel_1_wbsel;
  wire [2:0] controlmodel_1_immsel;
  wire [3:0] controlmodel_1_aluop, MemR;
  wire [31:0] adder_1_out, csr_1_csr, epc, immmodel_1_immdiate, multiplexer_2_out, multiplexer_3_out,
       multiplexer_4_out, multiplexer_5_out, multiplexer_6_out, npc, regfile_1_read_data_1, w2borh_1_dout;

  Adder #(.width(32)) adder_1 (.a(out_17), .b(32'h4), .out(adder_1_out));  // open: cin, cout
  // Probe on adder_1_out
  Multiplexer #(.select(1), .width(32), .disabled("Z"), .enable("false")) multiplexer_1 (
    .in0(adder_1_out), .in1(out_18), .out(npc), .sel(PCSel));
  and and_1 (intr1, mie, ~Zicsr, in_5);  // AND_Gate
  or or_1 (or_1_out, intr1, exc);
  Multiplexer #(.select(1), .width(32), .disabled("Z"), .enable("false")) multiplexer_2 (
    .in0(npc), .in1(32'h1c090000), .out(multiplexer_2_out), .sel(or_1_out));
  Register #(.width(32), .trigger("rising"), .Select("low")) PC (
    .D(multiplexer_3_out), .en(En), .Q(out_17), .clk(in_3));  // open: clr
  Multiplexer #(.select(1), .width(32), .disabled("Z"), .enable("false")) multiplexer_3 (
    .in0(multiplexer_2_out), .in1(epc), .out(multiplexer_3_out), .sel(trapRet));
  Comparator #(.width(32), .mode("unsigned")) comparator_1 (.a(in_1), .b({32{1'b0}}), .eq(out_8));  // open: gt, lt
  // Probe on out_17
  nor nor_1 (En, out_8, in_4);
  Pull_Resistor #(.pull(0)) pull_resistor_1 (.node(in_4));
  // Probe on in_1
  ControlModel controlmodel_1 (
    .BrUN(controlmodel_1_brun), .MemWrite(out_7), .ALUSelB(controlmodel_1_aluselb),
    .WBSel(controlmodel_1_wbsel), .RegWrite(controlmodel_1_regwrite), .ALUOP(controlmodel_1_aluop),
    .ImmSel(controlmodel_1_immsel), .JMP(controlmodel_1_jmp), .ALUSelA(controlmodel_1_alusela),
    .MemRead(MemR), .BEQ(controlmodel_1_beq), .BNE(controlmodel_1_bne), .BGE(controlmodel_1_bge),
    .BLT(controlmodel_1_blt), .BLTU(controlmodel_1_bltu), .BGEU(controlmodel_1_bgeu), .LoadSign(load_sign),
    .offset(out_18[1:0]), .opcode(in_1[6:0]), .funct3(in_1[14:12]), .funct7(in_1[31:25]), .trapRet(trapRet),
    .rs2(in_1[24:20]), .exception(exc), .Zicsr(Zicsr));
  ImmModel immmodel_1 (.Immdiate(immmodel_1_immdiate), .INSTRUCTION(in_1), .InstructionType(controlmodel_1_immsel));
  RegFile regfile_1 (
    .rs1(in_1[19:15]), .rs2(in_1[24:20]), .rd(in_1[11:7]), .Write_Data(multiplexer_6_out),
    .RegWE(controlmodel_1_regwrite), .clk(in_3), .Read_Data_1(regfile_1_read_data_1), .Read_Data_2(out_19),
    .ra(out_9), .sp(out_10), .t0(out_11), .t1(out_12), .t2(out_13), .s0(out_14), .s1(out_15), .a0(out_16));
  // Probe on out_19
  or or_2 (or_2_out, controlmodel_1_bge, controlmodel_1_bgeu);
  or or_3 (or_3_out, controlmodel_1_blt, controlmodel_1_bltu);
  Branch branch_1 (
    .BrEQ(branch_1_breq), .BrUN(controlmodel_1_brun), .RS1(regfile_1_read_data_1), .BrLT(branch_1_brlt),
    .RS2(out_19));
  Multiplexer #(.select(1), .width(32), .disabled("Z"), .enable("false")) multiplexer_4 (
    .in0(regfile_1_read_data_1), .in1(out_17), .out(multiplexer_4_out), .sel(controlmodel_1_alusela));
  Multiplexer #(.select(1), .width(32), .disabled("Z"), .enable("false")) multiplexer_5 (
    .in0(out_19), .in1(immmodel_1_immdiate), .out(multiplexer_5_out), .sel(controlmodel_1_aluselb));
  and and_2 (and_2_out, branch_1_breq, controlmodel_1_beq);
  and and_3 (and_3_out, ~branch_1_breq, controlmodel_1_bne);  // AND_Gate
  and and_4 (and_4_out, branch_1_brlt, or_3_out);
  and and_5 (and_5_out, ~branch_1_brlt, or_2_out);  // AND_Gate
  CSR csr_1 (
    .csrNo(in_1[31:20]), .intr(intr1), .clk(in_3), .wdin(immmodel_1_immdiate), .csr(csr_1_csr), .epc(epc),
    .pc(npc), .exc(exc), .mie(mie));
  or or_4 (PCSel, controlmodel_1_jmp, and_2_out, and_3_out, and_4_out, and_5_out);
  // Probe on out_18
  AluModel alumodel_1 (.ALUSel(controlmodel_1_aluop), .A(multiplexer_4_out), .B(multiplexer_5_out), .Result(out_18));
  or or_5 (out_6, MemR[0], MemR[1], MemR[2], MemR[3]);
  W2BorH w2borh_1 (.din(in_2), .mask(MemR), .dout(w2borh_1_dout), .\signed (load_sign));
  // Probe on w2borh_1_dout
  Multiplexer #(.select(2), .width(32), .disabled("Z"), .enable("false")) multiplexer_6 (
    .in0(adder_1_out), .in1(out_18), .in2(w2borh_1_dout), .in3(csr_1_csr), .out(multiplexer_6_out),
    .sel(controlmodel_1_wbsel));

  // Other names for the same wires on the sheet: a0[31:0] = out_16; clk = in_3; fetch_addr[31:0] = out_17;
  //   halt = out_8; Instruction[31:0] = in_1; intr = in_5; MemR1 = out_6; MemW[3:0] = out_7; Miss = in_4;
  //   ra[31:0] = out_9; ReadData[31:0] = in_2; s0[31:0] = out_14; s1[31:0] = out_15; sp[31:0] = out_10;
  //   t0[31:0] = out_11; t1[31:0] = out_12; t2[31:0] = out_13; WriteAddr[31:0] = out_18; WriteData[31:0] = out_19

  // Notes on the sheet:
  //   PC
  //   PC+4
  //   ALU_Result
  //   ALU_Result
  //   输入引脚区
  //   ALU_Result
  //   输出引脚区
  //   PC+4
  //   WriteData
  //   WBSel
endmodule

module ControlModel (
  input  [6:0] opcode,
  input  [1:0] offset,
  input  [2:0] funct3,
  input  [6:0] funct7,
  input  [4:0] rs2,
  output BrUN,
  output RegWrite,
  output JMP,
  output [2:0] ImmSel,
  output trapRet,
  output ALUSelA,
  output ALUSelB,
  output LoadSign,
  output [1:0] WBSel,
  output [3:0] MemWrite,
  output [3:0] ALUOP,
  output BEQ,
  output BLT,
  output Zicsr,
  output BNE,
  output BLTU,
  output [3:0] MemRead,
  output BGE,
  output BGEU,
  output exception
);

  wire and_13_out, and_19_out, and_20_out, and_21_out, and_22_out, and_23_out, and_24_out, and_26_out,
       comparator_2_eq, comparator_3_eq, comparator_4_eq, comparator_5_eq, comparator_6_eq, comparator_7_eq,
       comparator_8_eq, comparator_9_eq, comparator_10_eq, comparator_11_eq, comparator_12_eq,
       comparator_13_eq, comparator_18_eq, comparator_19_eq, comparator_20_eq, comparator_21_eq,
       comparator_22_eq, comparator_23_eq, comparator_24_eq, comparator_25_eq, comparator_26_eq,
       comparator_27_eq, comparator_28_eq, comparator_29_eq, comparator_30_eq, comparator_31_eq,
       comparator_32_eq, comparator_33_eq, comparator_34_eq, comparator_35_eq, comparator_36_eq,
       comparator_37_eq, comparator_38_eq, IType, JALR, lb, lbu, lh, lhu, Load, lw, or_2_out, or_4_out,
       or_5_out, or_6_out, or_7_out, or_10_out, or_16_out, or_17_out, or_18_out, or_19_out, RType, sb,
       SBType, sh, SType, sw, UJType, UType, Zicsr_I;
  wire [1:0] priority_encoder_3_out;
  wire [2:0] priority_encoder_4_out;
  wire [3:0] AOP_I, AOP_R, decoder_1_out0, decoder_2_out0, decoder_4_out0, decoder_5_out0, rom_2_data;

  Comparator #(.width(7), .mode("unsigned")) comparator_1 (.a(opcode), .b(7'b0110011), .eq(RType));  // open: gt, lt
  Comparator #(.width(7), .mode("unsigned")) comparator_2 (
    .a(opcode), .b(7'b0000011), .eq(comparator_2_eq));  // open: gt, lt
  Comparator #(.width(7), .mode("unsigned")) comparator_3 (
    .a(opcode), .b(7'b1100111), .eq(comparator_3_eq));  // open: gt, lt
  Comparator #(.width(7), .mode("unsigned")) comparator_4 (
    .a(opcode), .b(7'b0010011), .eq(comparator_4_eq));  // open: gt, lt
  Comparator #(.width(7), .mode("unsigned")) comparator_5 (
    .a(opcode), .b(7'b0000011), .eq(comparator_5_eq));  // open: gt, lt
  Comparator #(.width(3), .mode("unsigned")) comparator_6 (
    .a(funct3), .b(3'b000), .eq(comparator_6_eq));  // open: gt, lt
  Comparator #(.width(3), .mode("unsigned")) comparator_7 (
    .a(funct3), .b(3'b100), .eq(comparator_7_eq));  // open: gt, lt
  Comparator #(.width(3), .mode("unsigned")) comparator_8 (
    .a(funct3), .b(3'b001), .eq(comparator_8_eq));  // open: gt, lt
  Comparator #(.width(3), .mode("unsigned")) comparator_9 (
    .a(funct3), .b(3'b101), .eq(comparator_9_eq));  // open: gt, lt
  Comparator #(.width(3), .mode("unsigned")) comparator_10 (
    .a(funct3), .b(3'b010), .eq(comparator_10_eq));  // open: gt, lt
  and and_1 (Load, comparator_5_eq, IType);
  and and_2 (lb, Load, comparator_6_eq);
  and and_3 (sb, comparator_6_eq, SType);
  and and_4 (lbu, Load, comparator_7_eq);
  and and_5 (lh, Load, comparator_8_eq);
  and and_6 (sh, comparator_8_eq, SType);
  and and_7 (lhu, Load, comparator_9_eq);
  and and_8 (lw, Load, comparator_10_eq);
  and and_9 (sw, comparator_10_eq, SType);
  Comparator #(.width(3), .mode("unsigned")) comparator_11 (
    .a(funct3), .b(3'b000), .eq(comparator_11_eq));  // open: gt, lt
  Comparator #(.width(3), .mode("unsigned")) comparator_12 (
    .a(funct3), .b(3'b001), .eq(comparator_12_eq));  // open: gt, lt
  Comparator #(.width(3), .mode("unsigned")) comparator_13 (
    .a(funct3), .b(3'b101), .eq(comparator_13_eq));  // open: gt, lt
  or or_1 (IType, comparator_2_eq, comparator_3_eq, comparator_4_eq);
  and and_10 (BEQ, comparator_11_eq, SBType);
  and and_11 (BNE, comparator_12_eq, SBType);
  and and_12 (BGE, comparator_13_eq, SBType);
  Comparator #(.width(7), .mode("unsigned")) comparator_14 (.a(opcode), .b(7'b0110111), .eq(UType));  // open: gt, lt
  Comparator #(.width(7), .mode("unsigned")) comparator_15 (.a(opcode), .b(7'b1101111), .eq(UJType));  // open: gt, lt
  Comparator #(.width(7), .mode("unsigned")) comparator_16 (.a(opcode), .b(7'b0100011), .eq(SType));  // open: gt, lt
  Comparator #(.width(7), .mode("unsigned")) comparator_17 (.a(opcode), .b(7'b1100011), .eq(SBType));  // open: gt, lt
  Comparator #(.width(7), .mode("unsigned")) comparator_18 (
    .a(opcode), .b(7'b1100111), .eq(comparator_18_eq));  // open: gt, lt
  Comparator #(.width(7), .mode("unsigned")) comparator_19 (
    .a(opcode), .b(7'b1110011), .eq(comparator_19_eq));  // open: gt, lt
  Comparator #(.width(12), .mode("unsigned")) comparator_20 (
    .a({funct7, rs2}), .b(12'h102), .eq(comparator_20_eq));  // open: gt, lt
  or or_2 (or_2_out, comparator_20_eq, comparator_21_eq);
  Comparator #(.width(12), .mode("unsigned")) comparator_21 (
    .a({funct7, rs2}), .b(12'h302), .eq(comparator_21_eq));  // open: gt, lt
  or or_3 (LoadSign, lb, lh, lw);
  and and_13 (and_13_out, IType, ~JALR);  // AND_Gate
  Comparator #(.width(3), .mode("unsigned")) comparator_22 (
    .a(funct3), .b(3'b100), .eq(comparator_22_eq));  // open: gt, lt
  Comparator #(.width(3), .mode("unsigned")) comparator_23 (
    .a(funct3), .b(3'b110), .eq(comparator_23_eq));  // open: gt, lt
  Comparator #(.width(3), .mode("unsigned")) comparator_24 (
    .a(funct3), .b(3'b111), .eq(comparator_24_eq));  // open: gt, lt
  and and_14 (JALR, comparator_18_eq, IType);
  and and_15 (trapRet, comparator_19_eq, or_2_out);
  or or_4 (or_4_out, RType, and_13_out, UType);
  and and_16 (BLT, comparator_22_eq, SBType);
  and and_17 (BLTU, comparator_23_eq, SBType);
  and and_18 (BGEU, comparator_24_eq, SBType);
  or or_5 (or_5_out, UJType, JALR);
  or or_6 (or_6_out, or_5_out, or_4_out, Load, Zicsr);
  Pull_Resistor #(.pull(0)) pull_resistor_1 (.node(WBSel));
  Priority_Encoder #(.select(2), .disabled("Z")) priority_encoder_1 (
    .in0(or_5_out), .in1(or_4_out), .in2(Load), .in3(Zicsr), .out(WBSel), .en_in(or_6_out));  // open: gs, en_out
  Comparator #(.width(7), .mode("unsigned")) comparator_25 (
    .a(opcode), .b(7'b1110011), .eq(comparator_25_eq));  // open: gt, lt
  Comparator #(.width(3), .mode("unsigned")) comparator_26 (
    .a(funct3), .b(3'b001), .eq(comparator_26_eq));  // open: gt, lt
  Comparator #(.width(3), .mode("unsigned")) comparator_27 (
    .a(funct3), .b(3'b010), .eq(comparator_27_eq));  // open: gt, lt
  Comparator #(.width(3), .mode("unsigned")) comparator_28 (
    .a(funct3), .b(3'b011), .eq(comparator_28_eq));  // open: gt, lt
  Comparator #(.width(3), .mode("unsigned")) comparator_29 (
    .a(funct3), .b(3'b101), .eq(comparator_29_eq));  // open: gt, lt
  Comparator #(.width(3), .mode("unsigned")) comparator_30 (
    .a(funct3), .b(3'b110), .eq(comparator_30_eq));  // open: gt, lt
  Comparator #(.width(3), .mode("unsigned")) comparator_31 (
    .a(funct3), .b(3'b111), .eq(comparator_31_eq));  // open: gt, lt
  Comparator #(.width(7), .mode("unsigned")) comparator_32 (
    .a(opcode), .b(7'b1110011), .eq(comparator_32_eq));  // open: gt, lt
  Comparator #(.width(12), .mode("unsigned")) comparator_33 (
    .a({funct7, rs2}), .b({12{1'b0}}), .eq(comparator_33_eq));  // open: gt, lt
  Comparator #(.width(12), .mode("unsigned")) comparator_34 (
    .a({funct7, rs2}), .b(12'h1), .eq(comparator_34_eq));  // open: gt, lt
  Priority_Encoder #(.select(3), .disabled("Z")) priority_encoder_2 (
    .in0(IType), .in1(SType), .in2(SBType), .in3(UType), .in4(UJType), .in5(Zicsr_I), .out(ImmSel),
    .en_in(or_7_out));  // open: in6, in7, gs, en_out
  or or_7 (or_7_out, IType, SType, SBType, UType, UJType, Zicsr_I);
  or or_8 (ALUSelA, SBType, UJType);
  or or_9 (ALUSelB, IType, SType, SBType, UType, UJType);
  and and_19 (and_19_out, comparator_25_eq, comparator_26_eq);
  and and_20 (and_20_out, comparator_25_eq, comparator_27_eq);
  and and_21 (and_21_out, comparator_25_eq, comparator_28_eq);
  and and_22 (and_22_out, comparator_25_eq, comparator_29_eq);
  and and_23 (and_23_out, comparator_25_eq, comparator_30_eq);
  and and_24 (and_24_out, comparator_25_eq, comparator_31_eq);
  and and_25 (exception, comparator_32_eq, or_10_out);
  or or_10 (or_10_out, comparator_33_eq, comparator_34_eq);
  or or_11 (BrUN, BLTU, BGEU);
  or or_12 (RegWrite, RType, IType, UType, UJType, Zicsr);
  or or_13 (JMP, JALR, UJType);
  Pull_Resistor #(.pull(0)) pull_resistor_2 (.node(ImmSel));
  or or_14 (Zicsr, and_19_out, and_20_out, and_21_out, and_22_out, and_23_out, and_24_out);
  or or_15 (Zicsr_I, and_22_out, and_23_out, and_24_out);
  // Probe on JMP
  Decoder #(.select(2), .tristate("false"), .disabled(0), .enable("true")) decoder_1 (
    .out0(decoder_1_out0[0]), .out1(decoder_1_out0[1]), .out2(decoder_1_out0[2]), .out3(decoder_1_out0[3]),
    .sel(offset), .en(SType));
  Decoder #(.select(1), .tristate("false"), .disabled(0), .enable("true")) decoder_2 (
    .out0(decoder_2_out0[0]), .out1(decoder_2_out0[2]), .sel(offset[1]), .en(SType));
  Decoder #(.select(1), .tristate("false"), .disabled(0), .enable("true")) decoder_3 (
    .out0(decoder_2_out0[1]), .out1(decoder_2_out0[3]), .sel(offset[1]), .en(SType));
  Decoder #(.select(2), .tristate("false"), .disabled(0), .enable("true")) decoder_4 (
    .out0(decoder_4_out0[0]), .out1(decoder_4_out0[1]), .out2(decoder_4_out0[2]), .out3(decoder_4_out0[3]),
    .sel(offset), .en(Load));
  Decoder #(.select(1), .tristate("false"), .disabled(0), .enable("true")) decoder_5 (
    .out0(decoder_5_out0[0]), .out1(decoder_5_out0[2]), .sel(offset[1]), .en(Load));
  Decoder #(.select(1), .tristate("false"), .disabled(0), .enable("true")) decoder_6 (
    .out0(decoder_5_out0[1]), .out1(decoder_5_out0[3]), .sel(offset[1]), .en(Load));
  // Probe on opcode
  Comparator #(.width(7), .mode("unsigned")) comparator_35 (
    .a(7'b0010011), .b(opcode), .eq(comparator_35_eq));  // open: gt, lt
  Comparator #(.width(3), .mode("unsigned")) comparator_36 (
    .a(3'b101), .b(funct3), .eq(comparator_36_eq));  // open: gt, lt
  Comparator #(.width(7), .mode("unsigned")) comparator_37 (
    .a(7'b0100000), .b(funct7), .eq(comparator_37_eq));  // open: gt, lt
  Comparator #(.width(7), .mode("unsigned")) comparator_38 (
    .a(7'b0000011), .b(opcode), .eq(comparator_38_eq));  // open: gt, lt
  assign MemWrite = sb ? decoder_1_out0 : 4'bz;  // Controlled_Buffer controlled_buffer_1
  assign MemWrite = sh ? decoder_2_out0 : 4'bz;  // Controlled_Buffer controlled_buffer_2
  assign MemWrite = sw ? 4'b1111 : 4'bz;  // Controlled_Buffer controlled_buffer_3
  or or_16 (or_16_out, lb, lbu);
  assign MemRead = or_16_out ? decoder_4_out0 : 4'bz;  // Controlled_Buffer controlled_buffer_4
  or or_17 (or_17_out, lh, lhu);
  assign MemRead = or_17_out ? decoder_5_out0 : 4'bz;  // Controlled_Buffer controlled_buffer_5
  assign MemRead = lw ? 4'b1111 : 4'bz;  // Controlled_Buffer controlled_buffer_6
  // Probe on comparator_38_eq
  Pull_Resistor #(.pull(0)) pull_resistor_3 (.node(MemWrite));
  Pull_Resistor #(.pull(0)) pull_resistor_4 (.node(MemRead));
  ROM #(.addrWidth(10), .dataWidth(4), .Select("high")) rom_1 (.addr({funct3, funct7}), .data(AOP_R));
  ROM #(.addrWidth(3), .dataWidth(4), .Select("high")) rom_2 (.addr(funct3), .data(rom_2_data));
  // Probe on and_26_out
  and and_26 (and_26_out, comparator_35_eq, comparator_36_eq, comparator_37_eq);
  or or_18 (or_18_out, and_26_out, comparator_38_eq);
  Priority_Encoder #(.select(2), .disabled("Z")) priority_encoder_3 (
    .in1(and_26_out), .in2(comparator_38_eq), .out(priority_encoder_3_out), .en_in(or_18_out));  // open: in0, in3, gs, en_out
  // Probe on or_18_out
  // Probe on AOP_I
  Multiplexer #(.select(2), .width(4), .disabled("Z"), .enable("false")) multiplexer_1 (
    .in0(rom_2_data), .in1(4'b0101), .in2(4'b0000), .out(AOP_I), .sel(priority_encoder_3_out));  // open: in3
  Pull_Resistor #(.pull(0)) pull_resistor_5 (.node(priority_encoder_3_out));
  // Probe on priority_encoder_3_out
  Priority_Encoder #(.select(3), .disabled("Z")) priority_encoder_4 (
    .in0(RType), .in1(IType), .in2(SType), .in3(SBType), .in4(UType), .in5(UJType),
    .out(priority_encoder_4_out), .en_in(or_19_out));  // open: in6, in7, gs, en_out
  Pull_Resistor #(.pull(0)) pull_resistor_6 (.node(priority_encoder_4_out));
  or or_19 (or_19_out, RType, IType, SType, SBType, UType, UJType);
  // Probe on ALUOP
  Multiplexer #(.select(3), .width(4), .disabled("Z"), .enable("false")) multiplexer_2 (
    .in0(AOP_R), .in1(AOP_I), .in2(4'b0000), .in3(4'b0000), .in4(4'b1101), .in5(4'b0000), .out(ALUOP),
    .sel(priority_encoder_4_out));  // open: in6, in7
  // Probe on priority_encoder_4_out

  // Other names for the same wires on the sheet: inst_31_20[11:0] = {funct7, rs2}; AOP[3:0] = ALUOP;
  //   off_1 = offset[1]

  // Notes on the sheet:
  //   trapRet: pull=down
  //   exception: pull=down
  //   contents of rom_1 (hex, n*v repeats v):
  //   0 a c 12*0 f 16*0 c 95*0 6 e 126*0 7 128*0 b 126*0 3 127*0 4 8 30*0 5 95*0 2 127*0 1 9
  //   contents of rom_2 (hex, n*v repeats v):
  //   0 6 7 7 3 4 2 1
endmodule

module RegFile (
  input  [4:0] rs1,
  input  [4:0] rs2,
  input  [4:0] rd,
  input  [31:0] Write_Data,
  input  RegWE,
  input  clk,
  output [31:0] ra,
  output [31:0] sp,
  output [31:0] t0,
  output [31:0] t1,
  output [31:0] t2,
  output [31:0] s0,
  output [31:0] s1,
  output [31:0] a0,
  output [31:0] Read_Data_1,
  output [31:0] Read_Data_2
);

  wire write_en1, write_en2, write_en3, write_en4, write_en5, write_en6, write_en7, write_en8, write_en9,
       write_en10, write_en11, write_en12, write_en13, write_en14, write_en15, write_en16, write_en17,
       write_en18, write_en19, write_en20, write_en21, write_en22, write_en23, write_en24, write_en25,
       write_en26, write_en27, write_en28, write_en29, write_en30, write_en31;
  wire [31:0] a1, a2, a3, a4, a5, a6, a7, gp, s0_fp, s2, s3, s4, s5, s6, s7, s8, s9, s10, s11, t3, t4, t5,
       t6, tp;

  Pull_Resistor #(.pull(0)) pull_resistor_1 (.node(write_en1));
  Register #(.width(32), .trigger("rising"), .Select("low")) register_1 (
    .D(Write_Data), .en(write_en8), .Q(s0_fp), .clk(clk));  // open: clr
  Register #(.width(32), .trigger("rising"), .Select("low")) register_2 (
    .D(Write_Data), .en(write_en16), .Q(a6), .clk(clk));  // open: clr
  Register #(.width(32), .trigger("rising"), .Select("low")) register_3 (
    .D(Write_Data), .en(write_en24), .Q(s8), .clk(clk));  // open: clr
  Pull_Resistor #(.pull(0)) pull_resistor_2 (.node(write_en2));
  Pull_Resistor #(.pull(0)) pull_resistor_3 (.node(write_en3));
  Pull_Resistor #(.pull(0)) pull_resistor_4 (.node(write_en4));
  Pull_Resistor #(.pull(0)) pull_resistor_5 (.node(write_en5));
  // Probe on ra
  Register #(.width(32), .trigger("rising"), .Select("low")) register_4 (
    .D(Write_Data), .en(write_en1), .Q(ra), .clk(clk));  // open: clr
  Register #(.width(32), .trigger("rising"), .Select("low")) register_5 (
    .D(Write_Data), .en(write_en9), .Q(s1), .clk(clk));  // open: clr
  Register #(.width(32), .trigger("rising"), .Select("low")) register_6 (
    .D(Write_Data), .en(write_en17), .Q(a7), .clk(clk));  // open: clr
  Register #(.width(32), .trigger("rising"), .Select("low")) register_7 (
    .D(Write_Data), .en(write_en25), .Q(s9), .clk(clk));  // open: clr
  Pull_Resistor #(.pull(0)) pull_resistor_6 (.node(write_en7));
  Pull_Resistor #(.pull(0)) pull_resistor_7 (.node(write_en6));
  Pull_Resistor #(.pull(0)) pull_resistor_8 (.node(write_en8));
  Pull_Resistor #(.pull(0)) pull_resistor_9 (.node(write_en9));
  // Probe on Write_Data
  // Probe on write_en18
  Pull_Resistor #(.pull(0)) pull_resistor_10 (.node(write_en11));
  Pull_Resistor #(.pull(0)) pull_resistor_11 (.node(write_en10));
  Register #(.width(32), .trigger("rising"), .Select("low")) register_8 (
    .D(Write_Data), .en(write_en2), .Q(sp), .clk(clk));  // open: clr
  Register #(.width(32), .trigger("rising"), .Select("low")) register_9 (
    .D(Write_Data), .en(write_en10), .Q(a0), .clk(clk));  // open: clr
  // Probe on s2
  Register #(.width(32), .trigger("rising"), .Select("low")) register_10 (
    .D(Write_Data), .en(write_en18), .Q(s2), .clk(clk));  // open: clr
  Register #(.width(32), .trigger("rising"), .Select("low")) register_11 (
    .D(Write_Data), .en(write_en26), .Q(s10), .clk(clk));  // open: clr
  Pull_Resistor #(.pull(0)) pull_resistor_12 (.node(write_en12));
  Pull_Resistor #(.pull(0)) pull_resistor_13 (.node(write_en13));
  Pull_Resistor #(.pull(0)) pull_resistor_14 (.node(write_en14));
  Pull_Resistor #(.pull(0)) pull_resistor_15 (.node(write_en15));
  Register #(.width(32), .trigger("rising"), .Select("low")) register_12 (
    .D(Write_Data), .en(write_en3), .Q(gp), .clk(clk));  // open: clr
  Register #(.width(32), .trigger("rising"), .Select("low")) register_13 (
    .D(Write_Data), .en(write_en11), .Q(a1), .clk(clk));  // open: clr
  Register #(.width(32), .trigger("rising"), .Select("low")) register_14 (
    .D(Write_Data), .en(write_en19), .Q(s3), .clk(clk));  // open: clr
  Register #(.width(32), .trigger("rising"), .Select("low")) register_15 (
    .D(Write_Data), .en(write_en27), .Q(s11), .clk(clk));  // open: clr
  Pull_Resistor #(.pull(0)) pull_resistor_16 (.node(write_en16));
  Pull_Resistor #(.pull(0)) pull_resistor_17 (.node(write_en17));
  Pull_Resistor #(.pull(0)) pull_resistor_18 (.node(write_en18));
  Pull_Resistor #(.pull(0)) pull_resistor_19 (.node(write_en19));
  Register #(.width(32), .trigger("rising"), .Select("low")) register_16 (
    .D(Write_Data), .en(write_en4), .Q(tp), .clk(clk));  // open: clr
  Register #(.width(32), .trigger("rising"), .Select("low")) register_17 (
    .D(Write_Data), .en(write_en12), .Q(a2), .clk(clk));  // open: clr
  Register #(.width(32), .trigger("rising"), .Select("low")) register_18 (
    .D(Write_Data), .en(write_en20), .Q(s4), .clk(clk));  // open: clr
  Register #(.width(32), .trigger("rising"), .Select("low")) register_19 (
    .D(Write_Data), .en(write_en28), .Q(t3), .clk(clk));  // open: clr
  Pull_Resistor #(.pull(0)) pull_resistor_20 (.node(write_en20));
  Pull_Resistor #(.pull(0)) pull_resistor_21 (.node(write_en21));
  Pull_Resistor #(.pull(0)) pull_resistor_22 (.node(write_en22));
  Pull_Resistor #(.pull(0)) pull_resistor_23 (.node(write_en23));
  Decoder #(.select(5), .tristate("false"), .disabled("Z"), .enable("true")) decoder_1 (
    .out1(write_en1), .out2(write_en2), .out3(write_en3), .out4(write_en4), .out5(write_en5),
    .out6(write_en6), .out7(write_en7), .out8(write_en8), .out9(write_en9), .out10(write_en10),
    .out11(write_en11), .out12(write_en12), .out13(write_en13), .out14(write_en14), .out15(write_en15),
    .out16(write_en16), .out17(write_en17), .out18(write_en18), .out19(write_en19), .out20(write_en20),
    .out21(write_en21), .out22(write_en22), .out23(write_en23), .out24(write_en24), .out25(write_en25),
    .out26(write_en26), .out27(write_en27), .out28(write_en28), .out29(write_en29), .out30(write_en30),
    .out31(write_en31), .sel(rd), .en(RegWE));  // open: out0
  Register #(.width(32), .trigger("rising"), .Select("low")) register_20 (
    .D(Write_Data), .en(write_en5), .Q(t0), .clk(clk));  // open: clr
  Register #(.width(32), .trigger("rising"), .Select("low")) register_21 (
    .D(Write_Data), .en(write_en13), .Q(a3), .clk(clk));  // open: clr
  Register #(.width(32), .trigger("rising"), .Select("low")) register_22 (
    .D(Write_Data), .en(write_en21), .Q(s5), .clk(clk));  // open: clr
  Register #(.width(32), .trigger("rising"), .Select("low")) register_23 (
    .D(Write_Data), .en(write_en29), .Q(t4), .clk(clk));  // open: clr
  Pull_Resistor #(.pull(0)) pull_resistor_24 (.node(write_en24));
  // Probe on rd
  Pull_Resistor #(.pull(0)) pull_resistor_25 (.node(write_en25));
  Pull_Resistor #(.pull(0)) pull_resistor_26 (.node(write_en27));
  Pull_Resistor #(.pull(0)) pull_resistor_27 (.node(write_en26));
  Pull_Resistor #(.pull(0)) pull_resistor_28 (.node(write_en28));
  Register #(.width(32), .trigger("rising"), .Select("low")) register_24 (
    .D(Write_Data), .en(write_en6), .Q(t1), .clk(clk));  // open: clr
  Register #(.width(32), .trigger("rising"), .Select("low")) register_25 (
    .D(Write_Data), .en(write_en14), .Q(a4), .clk(clk));  // open: clr
  Register #(.width(32), .trigger("rising"), .Select("low")) register_26 (
    .D(Write_Data), .en(write_en22), .Q(s6), .clk(clk));  // open: clr
  // Probe on t5
  Register #(.width(32), .trigger("rising"), .Select("low")) register_27 (
    .D(Write_Data), .en(write_en30), .Q(t5), .clk(clk));  // open: clr
  Pull_Resistor #(.pull(0)) pull_resistor_29 (.node(write_en29));
  Pull_Resistor #(.pull(0)) pull_resistor_30 (.node(write_en30));
  Pull_Resistor #(.pull(0)) pull_resistor_31 (.node(write_en31));
  // Probe on Read_Data_1
  // Probe on rs1
  Register #(.width(32), .trigger("rising"), .Select("low")) register_28 (
    .D(Write_Data), .en(write_en7), .Q(t2), .clk(clk));  // open: clr
  Register #(.width(32), .trigger("rising"), .Select("low")) register_29 (
    .D(Write_Data), .en(write_en15), .Q(a5), .clk(clk));  // open: clr
  Register #(.width(32), .trigger("rising"), .Select("low")) register_30 (
    .D(Write_Data), .en(write_en23), .Q(s7), .clk(clk));  // open: clr
  Register #(.width(32), .trigger("rising"), .Select("low")) register_31 (
    .D(Write_Data), .en(write_en31), .Q(t6), .clk(clk));  // open: clr
  Multiplexer #(.select(5), .width(32), .disabled("Z"), .enable("false")) multiplexer_1 (
    .in0({32{1'b0}}), .in1(ra), .in2(sp), .in3(gp), .in4(tp), .in5(t0), .in6(t1), .in7(t2), .in8(s0_fp),
    .in9(s1), .in10(a0), .in11(a1), .in12(a2), .in13(a3), .in14(a4), .in15(a5), .in16(a6), .in17(a7),
    .in18(s2), .in19(s3), .in20(s4), .in21(s5), .in22(s6), .in23(s7), .in24(s8), .in25(s9), .in26(s10),
    .in27(s11), .in28(t3), .in29(t4), .in30(t5), .in31(t6), .out(Read_Data_1), .sel(rs1));
  // Probe on Read_Data_2
  // Probe on rs2
  Multiplexer #(.select(5), .width(32), .disabled("Z"), .enable("false")) multiplexer_2 (
    .in0({32{1'b0}}), .in1(ra), .in2(sp), .in3(gp), .in4(tp), .in5(t0), .in6(t1), .in7(t2), .in8(s0_fp),
    .in9(s1), .in10(a0), .in11(a1), .in12(a2), .in13(a3), .in14(a4), .in15(a5), .in16(a6), .in17(a7),
    .in18(s2), .in19(s3), .in20(s4), .in21(s5), .in22(s6), .in23(s7), .in24(s8), .in25(s9), .in26(s10),
    .in27(s11), .in28(t3), .in29(t4), .in30(t5), .in31(t6), .out(Read_Data_2), .sel(rs2));

  // Other names for the same wires on the sheet: read_data1[31:0] = Read_Data_1; read_data2[31:0] = Read_Data_2;
  //   read_reg1[4:0] = rs1; read_reg2[4:0] = rs2; write_en = RegWE; write_reg[4:0] = rd; x1[31:0] = ra; x2[31:0] = sp;
  //   x3[31:0] = gp; x4[31:0] = tp; x5[31:0] = t0; x6[31:0] = t1; x7[31:0] = t2; x8[31:0] = s0_fp; x9[31:0] = s1;
  //   x10[31:0] = a0; x11[31:0] = a1; x12[31:0] = a2; x13[31:0] = a3; x14[31:0] = a4; x15[31:0] = a5; x16[31:0] = a6;
  //   x17[31:0] = a7; x18[31:0] = s2; x19[31:0] = s3; x20[31:0] = s4; x21[31:0] = s5; x22[31:0] = s6; x23[31:0] = s7;
  //   x24[31:0] = s8; x25[31:0] = s9; x26[31:0] = s10; x27[31:0] = s11; x28[31:0] = t3; x29[31:0] = t4;
  //   x30[31:0] = t5; x31[31:0] = t6

  // Notes on the sheet:
  //   INPUTS to your circuit
  //   DON'T CHANGE THE LOCATIONS OF THE INPUTS AND OUTPUTS!
  //   These are DEBUG/TEST outputs from your circuit.
  //   OUTPUTS from your circuit
endmodule

module ImmModel (
  input  [31:0] INSTRUCTION,
  input  [2:0] InstructionType,
  output [31:0] Immdiate
);

  wire [31:0] bit_extender_1_out, bit_extender_2_out, bit_extender_3_out, bit_extender_4_out,
       bit_extender_5_out;

  // Probe on INSTRUCTION
  assign bit_extender_1_out = {{20{INSTRUCTION[31]}}, INSTRUCTION[31:20]};  // Bit_Extender bit_extender_1
  assign bit_extender_2_out = {{20{INSTRUCTION[31]}}, {INSTRUCTION[31:25], INSTRUCTION[11:7]}};  // Bit_Extender bit_extender_2
  assign bit_extender_3_out = {{19{INSTRUCTION[31]}}, {INSTRUCTION[31], INSTRUCTION[7], INSTRUCTION[30:25], INSTRUCTION[11:8], 1'b0}};  // Bit_Extender bit_extender_3
  // Probe on bit_extender_3_out
  assign bit_extender_4_out = {{11{INSTRUCTION[31]}}, {INSTRUCTION[31], INSTRUCTION[19:12], INSTRUCTION[20], INSTRUCTION[30:21], 1'b0}};  // Bit_Extender bit_extender_4
  assign bit_extender_5_out = {{27{1'b0}}, INSTRUCTION[19:15]};  // Bit_Extender bit_extender_5
  Multiplexer #(.select(3), .width(32), .disabled("Z"), .enable("false")) multiplexer_1 (
    .in0(bit_extender_1_out), .in1(bit_extender_2_out), .in2(bit_extender_3_out),
    .in3({INSTRUCTION[31:12], {12{1'b0}}}), .in4(bit_extender_4_out), .in5(bit_extender_5_out),
    .out(Immdiate), .sel(InstructionType));  // open: in6, in7

  // Notes on the sheet:
  //   I
  //   S
  //   U
  //   SB
  //   UJ
endmodule

module AluModel (
  input  [31:0] A,
  input  [31:0] B,
  input  [3:0] ALUSel,
  output [31:0] Result
);

  wire adder_3_cout, bitselector_1_out, bitselector_2_out, xor_1_out;
  wire [0:0] slt_alu;
  wire [15:0] adder_5_out, undriven, undriven_2;
  wire [31:0] add, adder_1_out, adder_3_out, and_alu, divu_alu, mul_alu, mulh_alu, mulhu_alu,
       multiplexer_1_out, multiplexer_2_out, multiplier_1_cout, multiplier_1_out, negator_1_out,
       negator_2_out, not_1_out, not_2_out, or_alu, remu_alu, sll_alu, sra_alu, srl_alu, sub_alu, xor_alu;
  wire [31:16] vaddh_alu;

  BitSelector #(.width(32), .group(1)) bitselector_1 (.in(A), .out(bitselector_1_out), .sel({5{1'b1}}));
  BitSelector #(.width(32), .group(1)) bitselector_2 (.in(B), .out(bitselector_2_out), .sel({5{1'b1}}));
  Negator #(.width(32)) negator_1 (.in(A), .out(negator_1_out));
  Negator #(.width(32)) negator_2 (.in(B), .out(negator_2_out));
  Multiplexer #(.select(1), .width(32), .disabled("Z"), .enable("false")) multiplexer_1 (
    .in0(A), .in1(negator_1_out), .out(multiplexer_1_out), .sel(bitselector_1_out));
  Multiplexer #(.select(1), .width(32), .disabled("Z"), .enable("false")) multiplexer_2 (
    .in0(B), .in1(negator_2_out), .out(multiplexer_2_out), .sel(bitselector_2_out));
  Multiplier #(.width(32)) multiplier_1 (
    .a(multiplexer_1_out), .b(multiplexer_2_out), .out(multiplier_1_out), .cout(multiplier_1_cout));  // open: cin
  xor xor_1 (xor_1_out, bitselector_1_out, bitselector_2_out);
  assign not_1_out = ~multiplier_1_out;  // NOT_Gate not_1, 32 bits wide
  Adder #(.width(32)) adder_1 (.a({32{1'b0}}), .b(not_2_out), .out(adder_1_out), .cin(adder_3_cout));  // open: cout
  assign not_2_out = ~multiplier_1_cout;  // NOT_Gate not_2, 32 bits wide
  Adder #(.width(32)) adder_2 (.a(A), .b(B), .out(add));  // open: cin, cout
  assign and_alu = A & B;  // AND_Gate and_1, 32 bits wide
  assign or_alu = A | B;  // OR_Gate or_1, 32 bits wide
  assign xor_alu = A ^ B;  // XOR_Gate xor_2, 32 bits wide
  Shifter #(.width(32), .shift("lr")) shifter_1 (.in(A), .\dist (B[4:0]), .out(srl_alu));
  Shifter #(.width(32), .shift("ar")) shifter_2 (.in(A), .\dist (B[4:0]), .out(sra_alu));
  Shifter #(.width(32), .shift("ll")) shifter_3 (.in(A), .\dist (B[4:0]), .out(sll_alu));
  Comparator #(.width(32), .mode("twosComplement")) comparator_1 (.a(A), .b(B), .lt(slt_alu[0]));  // open: gt, eq
  Adder #(.width(32)) adder_3 (.a(32'h1), .b(not_1_out), .out(adder_3_out), .cout(adder_3_cout));  // open: cin
  Multiplexer #(.select(1), .width(32), .disabled("Z"), .enable("false")) multiplexer_3 (
    .in0(multiplier_1_out), .in1(adder_3_out), .out(mul_alu), .sel(xor_1_out));
  Multiplexer #(.select(1), .width(32), .disabled("Z"), .enable("false")) multiplexer_4 (
    .in0(multiplier_1_cout), .in1(adder_1_out), .out(mulh_alu), .sel(xor_1_out));
  Divider #(.width(32)) divider_1 (.a(A), .b(B), .out(divu_alu), .rem(remu_alu));  // open: upper
  Multiplier #(.width(32)) multiplier_2 (.a(A), .b(B), .cout(mulhu_alu));  // open: out, cin
  Subtractor #(.width(32)) subtractor_1 (.a(A), .b(B), .out(sub_alu));  // open: bin, bout
  // Probe on Result
  Multiplexer #(.select(4), .width(32), .disabled("Z"), .enable("false")) multiplexer_5 (
    .in0(add), .in1(and_alu), .in2(or_alu), .in3(xor_alu), .in4(srl_alu), .in5(sra_alu), .in6(sll_alu),
    .in7({{31{1'b0}}, slt_alu[0]}), .in8(divu_alu), .in9(remu_alu), .in10(mul_alu), .in11(mulhu_alu),
    .in12(sub_alu), .in13(B), .in14(mulh_alu), .in15({vaddh_alu, vaddh_alu}), .out(Result), .sel(ALUSel));
  Adder #(.width(16)) adder_4 (.a(A[31:16]), .b(B[31:16]), .out(vaddh_alu));  // open: cin, cout
  Adder #(.width(16)) adder_5 (.a(undriven), .b(undriven_2), .out(adder_5_out));  // open: cin, cout

  // Other names for the same wires on the sheet: vaddh_alu[15:0] = vaddh_alu

  // Notes on the sheet:
  //   INPUTS to your circuit
  //   DON'T CHANGE THE LOCATIONS OF THE INPUTS AND OUTPUTS!
  //   OUTPUT from your circuit
endmodule

module Branch (
  input  [31:0] RS1,
  input  [31:0] RS2,
  input  BrUN,
  output BrEQ,
  output BrLT
);

  wire comparator_1_lt, comparator_2_lt;

  Comparator #(.width(32), .mode("twosComplement")) comparator_1 (
    .a(RS1), .b(RS2), .eq(BrEQ), .lt(comparator_1_lt));  // open: gt
  Comparator #(.width(32), .mode("unsigned")) comparator_2 (.a(RS1), .b(RS2), .lt(comparator_2_lt));  // open: gt, eq
  Multiplexer #(.select(1), .width(1), .disabled("Z"), .enable("false")) multiplexer_1 (
    .in0(comparator_1_lt), .in1(comparator_2_lt), .out(BrLT), .sel(BrUN));
endmodule

module IROM (
  input  [31:0] Program_counter,
  output [31:0] Instruction
);

  wire comparator_1_eq;
  wire [31:0] rom_1_data, rom_2_data;

  ROM #(.addrWidth(14), .dataWidth(32), .Select("high")) rom_1 (.addr(Program_counter[15:2]), .data(rom_1_data));
  ROM #(.addrWidth(14), .dataWidth(32), .Select("high")) rom_2 (.addr(Program_counter[15:2]), .data(rom_2_data));
  Comparator #(.width(16), .mode("twosComplement")) comparator_1 (
    .a(Program_counter[31:16]), .b(16'h1c09), .eq(comparator_1_eq));  // open: gt, lt
  Multiplexer #(.select(1), .width(32), .disabled("Z"), .enable("false")) multiplexer_1 (
    .in0(rom_1_data), .in1(rom_2_data), .out(Instruction), .sel(comparator_1_eq));

  // Notes on the sheet:
  //   Program_ROM
  //   Trap_Handler_ROM
  //   contents of rom_1 (hex, n*v repeats v):
  //   a06293 10000137 fffff4b7 254a223 204a283 704a303 28393 74a023 106593 feb316e3 74a023 704a303 206593
  //   feb31ae3 13f613 23f713 175713 a39793 1f7d793 1f3d813 e646b3 107c8b3 116c933 139393 12383b3 74a023
  //   704a303 306593 fcb314e3 fe010113 f3fe13 1c12023 43de93 fefe13 1c12223 83de93 fefe13 1c12423 c3de93
  //   fefe13 1c12623 103de93 fefe13 1c12823 143de93 fefe13 1c12a23 183de93 fefe13 1c12c23 1c3de93 fefe13
  //   1c12e23 700e13 e93 3ced463 2e9f13 2f0f33 f2f83 4f2703 efd663 ef2023 1ff2223 1e8e93 fddff06f fffe0e13
  //   fc0e58e3 12503 412583 812603 c12683 1012703 1412783 1812803 1c12883 1c89393 1881e93 1d3e3b3 1479e93
  //   1d3e3b3 1071e93 1d3e3b3 c69e93 1d3e3b3 861e93 1d3e3b3 459e93 1d3e3b3 a3e3b3 2010113 104d93 7b4a023
  //   6593 704a303 feb31ce3 74a023 6f
  //   contents of rom_2 (hex, n*v repeats v):
  //   30005073 fe810113 812a23 512823 612623 712423 1c12223 1d12023 fffff437 b00293 80000337 b30313
  //   342053f3 2538c63 4638063 fff06293 6542023 542023 1412403 1012283 c12303 812383 412e03 12e83 1810113
  //   30045073 30200073 6a42023 a42023 fd5ff06f 111112b7 11128293 11111337 11130313 888893b7 88838393
  //   f00e93 6542023 542023 e13 1e0e13 ffde6ee3 6282b3 fe53f4e3 f99ff06f
endmodule

module DRAM (
  input  [31:0] Write_Data,
  input  clk,
  input  Read_En,
  input  [31:0] Address,
  input  [3:0] Write_En,
  output [15:0] MissNubmer,
  output [31:0] Read_Data
);

  wire and_1_out, and_2_out, and_3_out, and_4_out, is_MemAddr, is_RomAddr, or_1_out, wreq;
  wire [15:0] controlled_buffer_3_out;
  wire [31:0] controlled_buffer_1_out, controlled_buffer_2_out, ram_data, rom_1_data, wdata_to_ram;

  Comparator #(.width(4), .mode("unsigned")) comparator_1 (
    .a(Address[31:28]), .b(4'b1000), .eq(is_RomAddr));  // open: gt, lt
  or or_1 (or_1_out, wreq, Read_En);
  not not_1 (is_MemAddr, is_RomAddr);
  and and_1 (and_1_out, or_1_out, is_MemAddr);
  assign controlled_buffer_1_out = and_1_out ? Address : 32'bz;  // Controlled_Buffer controlled_buffer_1
  assign controlled_buffer_2_out = and_2_out ? wdata_to_ram : 32'bz;  // Controlled_Buffer controlled_buffer_2
  and and_2 (and_2_out, wreq, is_MemAddr);
  assign controlled_buffer_3_out = is_RomAddr ? Address[17:2] : 16'bz;  // Controlled_Buffer controlled_buffer_3
  RAM #(.addrWidth(16), .dataWidth(32), .bus("separate"), .Select("high")) ram_1 (
    .addr(controlled_buffer_1_out[17:2]), .din(controlled_buffer_2_out), .data(ram_data), .str(and_2_out),
    .sel(1'b1), .clk(clk), .ld(1'b1));  // open: clr
  ROM #(.addrWidth(16), .dataWidth(32), .Select("high")) rom_1 (
    .addr(controlled_buffer_3_out), .data(rom_1_data), .sel(1'b1));
  or or_2 (wreq, Write_En[0], Write_En[1], Write_En[2], Write_En[3]);
  and and_3 (and_3_out, Read_En, is_MemAddr);
  assign Read_Data = and_3_out ? ram_data : 32'bz;  // Controlled_Buffer controlled_buffer_4
  assign Read_Data = and_4_out ? rom_1_data : 32'bz;  // Controlled_Buffer controlled_buffer_5
  and and_4 (and_4_out, Read_En, is_RomAddr);
  WrBorH wrborh_1 (.we(Write_En), .wdata_din(Write_Data), .ram_din(ram_data), .wdata_to_ram(wdata_to_ram));

  // Other names for the same wires on the sheet: Addr[31:0] = Address; MissNumber[15:0] = MissNubmer;
  //   ReadData[31:0] = Read_Data; ReadEnable = Read_En; rreq = Read_En; WriteData[31:0] = Write_Data;
  //   WriteEnable[3:0] = Write_En

  // Notes on the sheet:
  //   输入引脚区
  //   RAM
  //   二级存储器 ROM
  //   contents of rom_1 (hex, n*v repeats v):
  //   0 1 2 3 4 5 6 7 8 9 a b c d e f 10 11 12 13 14 15 16 17 18 19 1a 1b 1c 1d 1e 1f 20 21 22 23 24 25 26
  //   27 28 29 2a 2b 2c 2d 2e 2f 30 31 32 33 34 35 36 37 38 39 3a 3b 3c 3d 3e 3f 40 41 42 43 44 45 46 47
  //   48 49 4a 4b 4c 4d 4e 4f 50 51 52 53 54 55 56 57 58 59 5a 5b 5c 5d 5e 5f 60 61 62 63 64 65 66 67 68
  //   69 6a 6b 6c 6d 6e 6f 70 71 72 73 74 75 76 77 78 79 7a 7b 7c 7d 7e 7f ffffff80 ffffff81 ffffff82
  //   ffffff83 ffffff84 ffffff85 ffffff86 ffffff87 ffffff88 ffffff89 ffffff8a ffffff8b ffffff8c ffffff8d
  //   ffffff8e ffffff8f ffffff90 ffffff91 ffffff92 ffffff93 ffffff94 ffffff95 ffffff96 ffffff97 ffffff98
  //   ffffff99 ffffff9a ffffff9b ffffff9c ffffff9d ffffff9e ffffff9f ffffffa0 ffffffa1 ffffffa2 ffffffa3
  //   ffffffa4 ffffffa5 ffffffa6 ffffffa7 ffffffa8 ffffffa9 ffffffaa ffffffab ffffffac ffffffad ffffffae
  //   ffffffaf ffffffb0 ffffffb1 ffffffb2 ffffffb3 ffffffb4 ffffffb5 ffffffb6 ffffffb7 ffffffb8 ffffffb9
  //   ffffffba ffffffbb ffffffbc ffffffbd ffffffbe ffffffbf ffffffc0 ffffffc1 ffffffc2 ffffffc3 ffffffc4
  //   ffffffc5 ffffffc6 ffffffc7 ffffffc8 ffffffc9 ffffffca ffffffcb ffffffcc ffffffcd ffffffce ffffffcf
  //   ffffffd0 ffffffd1 ffffffd2 ffffffd3 ffffffd4 ffffffd5 ffffffd6 ffffffd7 ffffffd8 ffffffd9 ffffffda
  //   ffffffdb ffffffdc ffffffdd ffffffde ffffffdf ffffffe0 ffffffe1 ffffffe2 ffffffe3 ffffffe4 ffffffe5
  //   ffffffe6 ffffffe7 ffffffe8 ffffffe9 ffffffea ffffffeb ffffffec ffffffed ffffffee ffffffef fffffff0
  //   fffffff1 fffffff2 fffffff3 fffffff4 fffffff5 fffffff6 fffffff7 fffffff8 fffffff9 fffffffa fffffffb
  //   fffffffc fffffffd fffffffe ffffffff 0 1 2 3 4 5 6 7 8 9 a b c d e f 10 11 12 13 14 15 16 17 18 19 1a
  //   1b 1c 1d 1e 1f 20 21 22 23 24 25 26 27 28 29 2a 2b 2c 2d 2e 2f 30 31 32 33 34 35 36 37 38 39 3a 3b
  //   3c 3d 3e 3f 40 41 42 43 44 45 46 47 48 49 4a 4b 4c 4d 4e 4f 50 51 52 53 54 55 56 57 58 59 5a 5b 5c
  //   5d 5e 5f 60 61 62 63 64 65 66 67 68 69 6a 6b 6c 6d 6e 6f 70 71 72 73 74 75 76 77 78 79 7a 7b 7c 7d
  //   7e 7f ffffff80 ffffff81 ffffff82 ffffff83 ffffff84 ffffff85 ffffff86 ffffff87 ffffff88 ffffff89
  //   ffffff8a ffffff8b ffffff8c ffffff8d ffffff8e ffffff8f ffffff90 ffffff91 ffffff92 ffffff93 ffffff94
  //   ffffff95 ffffff96 ffffff97 ffffff98 ffffff99 ffffff9a ffffff9b ffffff9c ffffff9d ffffff9e ffffff9f
  //   ffffffa0 ffffffa1 ffffffa2 ffffffa3 ffffffa4 ffffffa5 ffffffa6 ffffffa7 ffffffa8 ffffffa9 ffffffaa
  //   ffffffab ffffffac ffffffad ffffffae ffffffaf ffffffb0 ffffffb1 ffffffb2 ffffffb3 ffffffb4 ffffffb5
  //   ffffffb6 ffffffb7 ffffffb8 ffffffb9 ffffffba ffffffbb ffffffbc ffffffbd ffffffbe ffffffbf ffffffc0
  //   ffffffc1 ffffffc2 ffffffc3 ffffffc4 ffffffc5 ffffffc6 ffffffc7 ffffffc8 ffffffc9 ffffffca ffffffcb
  //   ffffffcc ffffffcd ffffffce ffffffcf ffffffd0 ffffffd1 ffffffd2 ffffffd3 ffffffd4 ffffffd5 ffffffd6
  //   ffffffd7 ffffffd8 ffffffd9 ffffffda ffffffdb ffffffdc ffffffdd ffffffde ffffffdf ffffffe0 ffffffe1
  //   ffffffe2 ffffffe3 ffffffe4 ffffffe5 ffffffe6 ffffffe7 ffffffe8 ffffffe9 ffffffea ffffffeb ffffffec
  //   ffffffed ffffffee ffffffef fffffff0 fffffff1 fffffff2 fffffff3 fffffff4 fffffff5 fffffff6 fffffff7
  //   fffffff8 fffffff9 fffffffa fffffffb fffffffc fffffffd fffffffe ffffffff 0 1 2 3 4 5 6 7 8 9 a b c d
  //   e f 10 11 12 13 14 15 16 17 18 19 1a 1b 1c 1d 1e 1f 20 21 22 23 24 25 26 27 28 29 2a 2b 2c 2d 2e 2f
  //   30 31 32 33 34 35 36 37 38 39 3a 3b 3c 3d 3e 3f 40 41 42 43 44 45 46 47 48 49 4a 4b 4c 4d 4e 4f 50
  //   51 52 53 54 55 56 57 58 59 5a 5b 5c 5d 5e 5f 60 61 62 63 64 65 66 67 68 69 6a 6b 6c 6d 6e 6f 70 71
  //   72 73 74 75 76 77 78 79 7a 7b 7c 7d 7e 7f ffffff80 ffffff81 ffffff82 ffffff83 ffffff84 ffffff85
  //   ffffff86 ffffff87 ffffff88 ffffff89 ffffff8a ffffff8b ffffff8c ffffff8d ffffff8e ffffff8f ffffff90
  //   ffffff91 ffffff92 ffffff93 ffffff94 ffffff95 ffffff96 ffffff97 ffffff98 ffffff99 ffffff9a ffffff9b
  //   ffffff9c ffffff9d ffffff9e ffffff9f ffffffa0 ffffffa1 ffffffa2 ffffffa3 ffffffa4 ffffffa5 ffffffa6
  //   ffffffa7 ffffffa8 ffffffa9 ffffffaa ffffffab ffffffac ffffffad ffffffae ffffffaf ffffffb0 ffffffb1
  //   ffffffb2 ffffffb3 ffffffb4 ffffffb5 ffffffb6 ffffffb7 ffffffb8 ffffffb9 ffffffba ffffffbb ffffffbc
  //   ffffffbd ffffffbe ffffffbf ffffffc0 ffffffc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
  //   输出引脚区
endmodule

module WrBorH (
  input  [3:0] we,
  input  [31:0] wdata_din,
  input  [31:0] ram_din,
  output [31:0] wdata_to_ram
);

  wire wr_b0, wr_b1, wr_b2, wr_b3, wr_h0, wr_h1, wr_w;
  wire [31:0] and_1_out, and_2_out, and_3_out, and_4_out, and_5_out, and_6_out, and_7_out, and_8_out,
       controlled_buffer_1_out, or_1_out, shifter_1_out, shifter_2_out, shifter_3_out, shifter_4_out,
       wdata_from_cpu;

  Comparator #(.width(4), .mode("unsigned")) comparator_1 (.a(we), .b(4'b0001), .eq(wr_b0));  // open: gt, lt
  Comparator #(.width(4), .mode("unsigned")) comparator_2 (.a(we), .b(4'b0010), .eq(wr_b1));  // open: gt, lt
  Comparator #(.width(4), .mode("unsigned")) comparator_3 (.a(we), .b(4'b0100), .eq(wr_b2));  // open: gt, lt
  Comparator #(.width(4), .mode("unsigned")) comparator_4 (.a(we), .b(4'b1000), .eq(wr_b3));  // open: gt, lt
  Comparator #(.width(4), .mode("unsigned")) comparator_5 (.a(we), .b(4'b0011), .eq(wr_h0));  // open: gt, lt
  Comparator #(.width(4), .mode("unsigned")) comparator_6 (.a(we), .b(4'b1100), .eq(wr_h1));  // open: gt, lt
  Comparator #(.width(4), .mode("unsigned")) comparator_7 (.a(we), .b(4'b1111), .eq(wr_w));  // open: gt, lt
  assign and_1_out = wdata_din & 32'hff;  // AND_Gate and_1, 32 bits wide
  assign and_2_out = wdata_din & 32'hffff;  // AND_Gate and_2, 32 bits wide
  assign and_3_out = ram_din & 32'hffffff00;  // AND_Gate and_3, 32 bits wide
  assign and_4_out = ram_din & 32'hffff00ff;  // AND_Gate and_4, 32 bits wide
  assign and_5_out = ram_din & 32'hff00ffff;  // AND_Gate and_5, 32 bits wide
  assign and_6_out = ram_din & 32'hffffff;  // AND_Gate and_6, 32 bits wide
  assign and_7_out = ram_din & 32'hffff0000;  // AND_Gate and_7, 32 bits wide
  assign and_8_out = ram_din & 32'hffff;  // AND_Gate and_8, 32 bits wide
  Shifter #(.width(32), .shift("ll")) shifter_1 (.in(and_1_out), .\dist (5'b01000), .out(shifter_1_out));
  Shifter #(.width(32), .shift("ll")) shifter_2 (.in(and_1_out), .\dist (5'b10000), .out(shifter_2_out));
  Shifter #(.width(32), .shift("ll")) shifter_3 (.in(and_1_out), .\dist (5'b11000), .out(shifter_3_out));
  Shifter #(.width(32), .shift("ll")) shifter_4 (.in(and_2_out), .\dist (5'b10000), .out(shifter_4_out));
  assign controlled_buffer_1_out = wr_b0 ? and_3_out : 32'bz;  // Controlled_Buffer controlled_buffer_1
  assign controlled_buffer_1_out = wr_b1 ? and_4_out : 32'bz;  // Controlled_Buffer controlled_buffer_2
  assign controlled_buffer_1_out = wr_b2 ? and_5_out : 32'bz;  // Controlled_Buffer controlled_buffer_3
  assign controlled_buffer_1_out = wr_b3 ? and_6_out : 32'bz;  // Controlled_Buffer controlled_buffer_4
  assign controlled_buffer_1_out = wr_h0 ? and_7_out : 32'bz;  // Controlled_Buffer controlled_buffer_5
  assign controlled_buffer_1_out = wr_h1 ? and_8_out : 32'bz;  // Controlled_Buffer controlled_buffer_6
  assign wdata_from_cpu = wr_b0 ? and_1_out : 32'bz;  // Controlled_Buffer controlled_buffer_7
  assign wdata_from_cpu = wr_b1 ? shifter_1_out : 32'bz;  // Controlled_Buffer controlled_buffer_8
  assign wdata_from_cpu = wr_b2 ? shifter_2_out : 32'bz;  // Controlled_Buffer controlled_buffer_9
  assign wdata_from_cpu = wr_b3 ? shifter_3_out : 32'bz;  // Controlled_Buffer controlled_buffer_10
  assign wdata_from_cpu = wr_h0 ? and_2_out : 32'bz;  // Controlled_Buffer controlled_buffer_11
  assign wdata_from_cpu = wr_h1 ? shifter_4_out : 32'bz;  // Controlled_Buffer controlled_buffer_12
  assign wdata_from_cpu = wr_w ? wdata_din : 32'bz;  // Controlled_Buffer controlled_buffer_13
  assign or_1_out = controlled_buffer_1_out | wdata_from_cpu;  // OR_Gate or_1, 32 bits wide
  Multiplexer #(.select(1), .width(32), .disabled("Z"), .enable("false")) multiplexer_1 (
    .in0(or_1_out), .in1(wdata_from_cpu), .out(wdata_to_ram), .sel(wr_w));
endmodule

module W2BorH (
  input  [31:0] din,
  input  \signed ,
  input  [3:0] mask,
  output [31:0] dout
);

  wire comparator_1_eq, comparator_2_eq, comparator_3_eq, comparator_4_eq, comparator_5_eq, comparator_6_eq,
       comparator_7_eq;
  wire [31:0] and_1_out, and_2_out, and_3_out, and_5_out, byte0, byte0_sext, byte0_uext, byte1, byte1_sext,
       byte1_uext, byte2, byte2_sext, byte2_uext, byte3, byte3_sext, byte3_uext, halfw0, halfw0_sext,
       halfw0_uext, halfw1, halfw1_sext, halfw1_uext;

  assign and_1_out = din & 32'hff;  // AND_Gate and_1, 32 bits wide
  assign and_2_out = din & 32'hff00;  // AND_Gate and_2, 32 bits wide
  assign and_3_out = din & 32'hff0000;  // AND_Gate and_3, 32 bits wide
  assign byte3 = din & 32'hff000000;  // AND_Gate and_4, 32 bits wide
  assign and_5_out = din & 32'hffff;  // AND_Gate and_5, 32 bits wide
  assign halfw1 = din & 32'hffff0000;  // AND_Gate and_6, 32 bits wide
  Comparator #(.width(4), .mode("unsigned")) comparator_1 (
    .a(mask), .b(4'b0001), .eq(comparator_1_eq));  // open: gt, lt
  Comparator #(.width(4), .mode("unsigned")) comparator_2 (
    .a(mask), .b(4'b0010), .eq(comparator_2_eq));  // open: gt, lt
  Comparator #(.width(4), .mode("unsigned")) comparator_3 (
    .a(mask), .b(4'b0100), .eq(comparator_3_eq));  // open: gt, lt
  Comparator #(.width(4), .mode("unsigned")) comparator_4 (
    .a(mask), .b(4'b1000), .eq(comparator_4_eq));  // open: gt, lt
  Comparator #(.width(4), .mode("unsigned")) comparator_5 (
    .a(mask), .b(4'b0011), .eq(comparator_5_eq));  // open: gt, lt
  Comparator #(.width(4), .mode("unsigned")) comparator_6 (
    .a(mask), .b(4'b1100), .eq(comparator_6_eq));  // open: gt, lt
  Comparator #(.width(4), .mode("unsigned")) comparator_7 (
    .a(mask), .b(4'b1111), .eq(comparator_7_eq));  // open: gt, lt
  Shifter #(.width(32), .shift("ll")) shifter_1 (.in(and_1_out), .\dist (5'b11000), .out(byte0));
  Shifter #(.width(32), .shift("ll")) shifter_2 (.in(and_2_out), .\dist (5'b10000), .out(byte1));
  Shifter #(.width(32), .shift("ll")) shifter_3 (.in(and_3_out), .\dist (5'b01000), .out(byte2));
  Shifter #(.width(32), .shift("ll")) shifter_4 (.in(and_5_out), .\dist (5'b10000), .out(halfw0));
  Multiplexer #(.select(1), .width(32), .disabled("Z"), .enable("true")) multiplexer_1 (
    .in0(byte0_uext), .in1(byte0_sext), .out(dout), .sel(\signed ), .en(comparator_1_eq));
  Multiplexer #(.select(1), .width(32), .disabled("Z"), .enable("true")) multiplexer_2 (
    .in0(byte1_uext), .in1(byte1_sext), .out(dout), .sel(\signed ), .en(comparator_2_eq));
  Multiplexer #(.select(1), .width(32), .disabled("Z"), .enable("true")) multiplexer_3 (
    .in0(byte2_uext), .in1(byte2_sext), .out(dout), .sel(\signed ), .en(comparator_3_eq));
  Multiplexer #(.select(1), .width(32), .disabled("Z"), .enable("true")) multiplexer_4 (
    .in0(byte3_uext), .in1(byte3_sext), .out(dout), .sel(\signed ), .en(comparator_4_eq));
  Multiplexer #(.select(1), .width(32), .disabled("Z"), .enable("true")) multiplexer_5 (
    .in0(halfw0_uext), .in1(halfw0_sext), .out(dout), .sel(\signed ), .en(comparator_5_eq));
  Multiplexer #(.select(1), .width(32), .disabled("Z"), .enable("true")) multiplexer_6 (
    .in0(halfw1_uext), .in1(halfw1_sext), .out(dout), .sel(\signed ), .en(comparator_6_eq));
  assign dout = comparator_7_eq ? din : 32'bz;  // Controlled_Buffer controlled_buffer_1
  Shifter #(.width(32), .shift("lr")) shifter_5 (.in(byte0), .\dist (5'b11000), .out(byte0_uext));
  Shifter #(.width(32), .shift("ar")) shifter_6 (.in(byte0), .\dist (5'b11000), .out(byte0_sext));
  Shifter #(.width(32), .shift("lr")) shifter_7 (.in(byte1), .\dist (5'b11000), .out(byte1_uext));
  Shifter #(.width(32), .shift("ar")) shifter_8 (.in(byte1), .\dist (5'b11000), .out(byte1_sext));
  Shifter #(.width(32), .shift("lr")) shifter_9 (.in(byte2), .\dist (5'b11000), .out(byte2_uext));
  Shifter #(.width(32), .shift("ar")) shifter_10 (.in(byte2), .\dist (5'b11000), .out(byte2_sext));
  Shifter #(.width(32), .shift("lr")) shifter_11 (.in(byte3), .\dist (5'b11000), .out(byte3_uext));
  Shifter #(.width(32), .shift("ar")) shifter_12 (.in(byte3), .\dist (5'b11000), .out(byte3_sext));
  Shifter #(.width(32), .shift("lr")) shifter_13 (.in(halfw0), .\dist (5'b10000), .out(halfw0_uext));
  Shifter #(.width(32), .shift("ar")) shifter_14 (.in(halfw0), .\dist (5'b10000), .out(halfw0_sext));
  Shifter #(.width(32), .shift("lr")) shifter_15 (.in(halfw1), .\dist (5'b10000), .out(halfw1_uext));
  Shifter #(.width(32), .shift("ar")) shifter_16 (.in(halfw1), .\dist (5'b10000), .out(halfw1_sext));

  // Other names for the same wires on the sheet: sign = \signed ; word[31:0] = din
endmodule

module CSR (
  input  [11:0] csrNo,
  input  [31:0] pc,
  input  [31:0] wdin,
  input  clk,
  input  intr,
  input  exc,
  output [31:0] csr,
  output [31:0] epc,
  output mie
);

  wire mcause, mepc, mstatus, or_1_out, or_2_out;
  wire [31:0] mcause_q, mstatus_q, multiplexer_1_out, multiplexer_2_out;

  Comparator #(.width(12), .mode("twosComplement")) comparator_1 (
    .a(12'h300), .b(csrNo), .eq(mstatus));  // open: gt, lt
  Comparator #(.width(12), .mode("twosComplement")) comparator_2 (.a(12'h341), .b(csrNo), .eq(mepc));  // open: gt, lt
  Comparator #(.width(12), .mode("twosComplement")) comparator_3 (.a(12'h342), .b(csrNo), .eq(mcause));  // open: gt, lt
  Multiplexer #(.select(1), .width(32), .disabled("Z"), .enable("false")) multiplexer_1 (
    .in0(pc), .in1(wdin), .out(multiplexer_1_out), .sel(mepc));
  or or_1 (or_1_out, mepc, intr, exc);
  Multiplexer #(.select(1), .width(32), .disabled("Z"), .enable("false")) multiplexer_2 (
    .in0({intr, 31'hb}), .in1(wdin), .out(multiplexer_2_out), .sel(mcause));
  or or_2 (or_2_out, mcause, intr, exc);
  Register #(.width(32), .trigger("rising"), .Select("low")) u_mstatus (
    .D(wdin), .en(mstatus), .Q({mstatus_q[31:4], mie, mstatus_q[2:0]}), .clk(clk));  // open: clr
  Register #(.width(32), .trigger("rising"), .Select("low")) u_mepc (
    .D(multiplexer_1_out), .en(or_1_out), .Q(epc), .clk(clk));  // open: clr
  Register #(.width(32), .trigger("rising"), .Select("low")) u_mcause (
    .D(multiplexer_2_out), .en(or_2_out), .Q(mcause_q), .clk(clk));  // open: clr
  assign csr = mstatus ? {mstatus_q[31:4], mie, mstatus_q[2:0]} : 32'bz;  // Controlled_Buffer controlled_buffer_1
  assign csr = mepc ? epc : 32'bz;  // Controlled_Buffer controlled_buffer_2
  assign csr = mcause ? mcause_q : 32'bz;  // Controlled_Buffer controlled_buffer_3

  // Other names for the same wires on the sheet: npc[31:0] = pc
endmodule

module IOBus (
  input  [31:0] WriteAddr,
  input  [31:0] WriteData,
  input  R,
  input  [3:0] W,
  input  [31:0] IOReadData,
  input  [31:0] MemRead,
  output [31:0] ReadData,
  output [3:0] IOWe,
  output IOEn,
  output [11:0] IOAddr12,
  output [31:0] IOWriteData,
  output [31:0] MemAddr,
  output MemR,
  output [3:0] MemW,
  output [31:0] MemWriteData
);

  wire and_2_out, and_3_out, and_4_out, and_5_out, is_MemAddr, is_PeriAddr, or_2_out, or_3_out, wreq;
  wire [3:0] controlled_buffer_4_out;

  // Probe on WriteAddr
  assign MemW = is_MemAddr ? W : 4'bz;  // Controlled_Buffer controlled_buffer_1
  or or_1 (wreq, W[0], W[1], W[2], W[3]);
  Comparator #(.width(20), .mode("unsigned")) comparator_1 (
    .a(WriteAddr[31:12]), .b({20{1'b1}}), .eq(is_PeriAddr));  // open: gt, lt
  assign MemR = is_MemAddr ? R : 1'bz;  // Controlled_Buffer controlled_buffer_2
  // Probe on is_PeriAddr
  not not_1 (is_MemAddr, is_PeriAddr);
  and and_1 (IOEn, is_PeriAddr, or_2_out);
  or or_2 (or_2_out, wreq, R);
  or or_3 (or_3_out, wreq, R);
  and and_2 (and_2_out, is_MemAddr, or_3_out);
  // Probe on WriteAddr
  assign MemAddr = and_2_out ? WriteAddr : 32'bz;  // Controlled_Buffer controlled_buffer_3
  // Probe on MemAddr
  assign controlled_buffer_4_out = wreq ? W : 4'bz;  // Controlled_Buffer controlled_buffer_4
  assign IOWe = is_PeriAddr ? controlled_buffer_4_out : 4'bz;  // Controlled_Buffer controlled_buffer_5
  and and_3 (and_3_out, is_MemAddr, wreq);
  assign MemWriteData = and_3_out ? WriteData : 32'bz;  // Controlled_Buffer controlled_buffer_6
  Pull_Resistor #(.pull(0)) pull_resistor_1 (.node(IOWe));
  and and_4 (and_4_out, R, IOEn);
  assign ReadData = and_4_out ? IOReadData : 32'bz;  // Controlled_Buffer controlled_buffer_7
  assign ReadData = and_5_out ? MemRead : 32'bz;  // Controlled_Buffer controlled_buffer_8
  and and_5 (and_5_out, R, is_MemAddr);
  // Probe on ReadData

  assign IOAddr12 = WriteAddr[11:0];
  assign IOWriteData = WriteData;

  // Other names for the same wires on the sheet: rreq = R
endmodule

module DigitDriver (
  input  in_1,
  input  IOEn,
  input  [31:0] IOWriteData,
  input  [3:0] IOWe,
  input  [11:0] IOAddr12,
  output [3:0] D0,
  output [3:0] D4,
  output [3:0] D1,
  output [3:0] D5,
  output [3:0] D2,
  output [3:0] D6,
  output [3:0] D3,
  output [3:0] D7
);

  wire and_1_out, comparator_1_eq;
  wire [31:0] controlled_buffer_1_out, wd2LED;

  Comparator #(.width(10), .mode("unsigned")) comparator_1 (
    .a({10{1'b0}}), .b(IOAddr12[11:2]), .eq(comparator_1_eq));  // open: gt, lt
  // Probe on IOEn
  // Probe on and_1_out
  and and_1 (and_1_out, comparator_1_eq, IOEn);
  // Probe on {D7, D6, D5, D4, D3, D2, D1, D0}
  WrBorH wrborh_1 (
    .we(IOWe), .wdata_din(IOWriteData), .ram_din({D7, D6, D5, D4, D3, D2, D1, D0}), .wdata_to_ram(wd2LED));
  // Probe on wd2LED
  assign controlled_buffer_1_out = and_1_out ? wd2LED : 32'bz;  // Controlled_Buffer controlled_buffer_1
  // Probe on controlled_buffer_1_out[3:0]
  // Probe on D0
  Register #(.width(4), .trigger("rising"), .Select("low")) register_1 (
    .D(controlled_buffer_1_out[3:0]), .en(and_1_out), .Q(D0), .clk(in_1));  // open: clr
  Register #(.width(4), .trigger("rising"), .Select("low")) register_2 (
    .D(controlled_buffer_1_out[7:4]), .en(and_1_out), .Q(D1), .clk(in_1));  // open: clr
  Register #(.width(4), .trigger("rising"), .Select("low")) register_3 (
    .D(controlled_buffer_1_out[11:8]), .en(and_1_out), .Q(D2), .clk(in_1));  // open: clr
  Register #(.width(4), .trigger("rising"), .Select("low")) register_4 (
    .D(controlled_buffer_1_out[15:12]), .en(and_1_out), .Q(D3), .clk(in_1));  // open: clr
  Register #(.width(4), .trigger("rising"), .Select("low")) register_5 (
    .D(controlled_buffer_1_out[19:16]), .en(and_1_out), .Q(D4), .clk(in_1));  // open: clr
  Register #(.width(4), .trigger("rising"), .Select("low")) register_6 (
    .D(controlled_buffer_1_out[23:20]), .en(and_1_out), .Q(D5), .clk(in_1));  // open: clr
  Register #(.width(4), .trigger("rising"), .Select("low")) register_7 (
    .D(controlled_buffer_1_out[27:24]), .en(and_1_out), .Q(D6), .clk(in_1));  // open: clr
  Register #(.width(4), .trigger("rising"), .Select("low")) register_8 (
    .D(controlled_buffer_1_out[31:28]), .en(and_1_out), .Q(D7), .clk(in_1));  // open: clr

  // Other names for the same wires on the sheet: clk = in_1; IOBase[9:0] = IOAddr12[11:2];
  //   LEDdata[31:0] = {D7, D6, D5, D4, D3, D2, D1, D0}; We[3:0] = IOWe

  // Notes on the sheet:
  //   输入管脚
  //   输出管脚
endmodule

module LEDDriver (
  input  in_1,
  input  IOEn,
  input  [31:0] IOWriteData,
  input  [3:0] IOWe,
  input  [11:0] IOAddr12,
  output [23:0] LED0
);

  wire and_1_out, comparator_1_eq;
  wire [23:0] controlled_buffer_1_out;
  wire [31:0] wd2LED;

  Comparator #(.width(10), .mode("unsigned")) comparator_1 (
    .a(10'h18), .b(IOAddr12[11:2]), .eq(comparator_1_eq));  // open: gt, lt
  // Probe on IOEn
  // Probe on and_1_out
  and and_1 (and_1_out, comparator_1_eq, IOEn);
  WrBorH wrborh_1 (.we(IOWe), .wdata_din(IOWriteData), .ram_din({{8{1'b0}}, LED0}), .wdata_to_ram(wd2LED));
  assign controlled_buffer_1_out = and_1_out ? wd2LED[23:0] : 24'bz;  // Controlled_Buffer controlled_buffer_1
  // Probe on controlled_buffer_1_out
  Register #(.width(24), .trigger("rising"), .Select("low")) register_1 (
    .D(controlled_buffer_1_out), .en(and_1_out), .Q(LED0), .clk(in_1));  // open: clr

  // Other names for the same wires on the sheet: clk = in_1; IOBase[9:0] = IOAddr12[11:2]; We[3:0] = IOWe

  // Notes on the sheet:
  //   输入管脚
  //   输出管脚
endmodule

module SwitchDriver (
  input  in_1,
  input  [23:0] SW0,
  input  IOEn,
  input  [11:0] IOAddr12,
  output [31:0] IOReadData
);

  wire and_1_out, comparator_1_eq;
  wire [31:0] multiplexer_1_out;

  Comparator #(.width(10), .mode("unsigned")) comparator_1 (
    .a(10'h1c), .b(IOAddr12[11:2]), .eq(comparator_1_eq));  // open: gt, lt
  and and_1 (and_1_out, comparator_1_eq, IOEn);
  Multiplexer #(.select(1), .width(32), .disabled("Z"), .enable("false")) multiplexer_1 (
    .in1({{8{1'b0}}, SW0}), .out(multiplexer_1_out), .sel(and_1_out));  // open: in0
  assign IOReadData = and_1_out ? multiplexer_1_out : 32'bz;  // Controlled_Buffer controlled_buffer_1

  // Other names for the same wires on the sheet: clk = in_1; IOBase[9:0] = IOAddr12[11:2]

  // Notes on the sheet:
  //   输入管脚
  //   输出管脚
endmodule

module Timer (
  input  in_1,
  input  IOEn,
  input  [31:0] IOWriteData,
  input  [3:0] IOWe,
  input  [11:0] IOAddr12,
  output [31:0] IOReadData
);

  wire and_1_out, and_2_out, and_3_out, comparator_1_eq, comparator_2_eq, threshold_reached, We;
  wire [31:0] counter_1_q, threshold_q, timer_q;

  Comparator #(.width(10), .mode("unsigned")) comparator_1 (
    .a(10'h8), .b(IOAddr12[11:2]), .eq(comparator_1_eq));  // open: gt, lt
  Comparator #(.width(10), .mode("unsigned")) comparator_2 (
    .a(10'h9), .b(IOAddr12[11:2]), .eq(comparator_2_eq));  // open: gt, lt
  and and_1 (and_1_out, comparator_1_eq, IOEn);
  and and_2 (and_2_out, We, comparator_2_eq, IOEn);
  and and_3 (and_3_out, We, and_1_out);
  Register #(.width(32), .trigger("rising"), .Select("low")) threshold (
    .D(IOWriteData), .en(and_2_out), .Q(threshold_q), .clk(in_1));  // open: clr
  Counter #(.width(32), .max('hffffffff), .ongoal("wrap"), .trigger("rising"), .behavior("new")) counter_1 (
    .load(threshold_reached), .D({32{1'b0}}), .Q(counter_1_q), .clk(in_1));  // open: count, carry, clr, preset, down
  or or_1 (We, IOWe[0], IOWe[1], IOWe[2], IOWe[3]);
  Comparator #(.width(32), .mode("twosComplement")) comparator_3 (
    .a(threshold_q), .b(counter_1_q), .eq(threshold_reached));  // open: gt, lt
  Counter #(.width(32), .max('hffffffff), .ongoal("wrap"), .trigger("rising"), .behavior("new")) timer (
    .load(and_3_out), .D(IOWriteData), .count(threshold_reached), .Q(timer_q), .clk(in_1));  // open: carry, clr, preset, down
  assign IOReadData = and_1_out ? timer_q : 32'bz;  // Controlled_Buffer controlled_buffer_1

  // Other names for the same wires on the sheet: clk = in_1; IOBase[9:0] = IOAddr12[11:2]; timer[31:0] = IOReadData

  // Notes on the sheet:
  //   输入管脚
  //   输出管脚
endmodule

module debug (
  input  [31:0] PC,
  input  [31:0] brkPC,
  input  clr,
  input  clk_i,
  output clk_o
);

  wire and_1_out, comparator_1_eq;

  Comparator #(.width(32), .mode("twosComplement")) comparator_1 (
    .a(PC), .b(brkPC), .eq(comparator_1_eq));  // open: gt, lt
  Pull_Resistor #(.pull(0)) pull_resistor_1 (.node(clr));
  and and_1 (and_1_out, comparator_1_eq, ~clr);  // AND_Gate
  and and_2 (clk_o, ~and_1_out, clk_i);  // AND_Gate
endmodule
